// Digital circuit FSM.dig as structural Verilog
module FSM (
  input  fsm_tick,
  output Q_0,
  output Q_1,
  output [7:0] out_counter,
  output change_of_state
);

  wire and_3_out, and_4_out, and_5_out, and_6_out, and_7_out, and_8_out, D0_q, D1_q, IF_0_gt, IF_1_gt,
       IF_2_gt, multiplexer_1_out, multiplexer_2_out, not_1_out, not_2_out, not_3_out, not_4_out;

  D_FF D0 (.D(multiplexer_1_out), .C(fsm_tick), .Q(D0_q));  // open: nQ
  D_FF D1 (.D(multiplexer_2_out), .C(fsm_tick), .Q(D1_q));  // open: nQ
  Multiplexer multiplexer_1 (.sel(change_of_state), .in_0(D0_q), .in_1(Q_0), .out(multiplexer_1_out));
  Multiplexer multiplexer_2 (.sel(change_of_state), .in_0(D1_q), .in_1(Q_1), .out(multiplexer_2_out));
  not not_1 (not_1_out, D0_q);
  not not_2 (not_2_out, D1_q);
  CounterPreset #(.maxValue(255), .Bits(8)) counterpreset_1 (
    .en(1'b1), .C(fsm_tick), .dir(1'b0), .in({8{1'b0}}), .ld(change_of_state), .clr(change_of_state),
    .out(out_counter));  // open: ovf
  and and_1 (Q_0, not_1_out, not_2_out);
  and and_2 (Q_1, D0_q, not_2_out);
  not not_3 (not_3_out, Q_0);
  not not_4 (not_4_out, Q_1);
  and and_3 (and_3_out, Q_0, not_4_out);
  and and_4 (and_4_out, Q_1, not_3_out);
  and and_5 (and_5_out, not_3_out, not_4_out);
  Comparator #(.Bits(8)) IF_2 (.a(out_counter), .b(8'ha), .gt(IF_2_gt));  // open: eq, lt
  Comparator #(.Bits(8)) IF_1 (.a(out_counter), .b(8'h3), .gt(IF_1_gt));  // open: eq, lt
  Comparator #(.Bits(8)) IF_0 (.a(out_counter), .b(8'h6), .gt(IF_0_gt));  // open: eq, lt
  LED S_2 (.in(and_5_out));
  and and_6 (and_6_out, and_5_out, IF_2_gt);
  LED S_1 (.in(and_4_out));
  and and_7 (and_7_out, and_4_out, IF_1_gt);
  LED S_0 (.in(and_3_out));
  and and_8 (and_8_out, and_3_out, IF_0_gt);
  or or_1 (change_of_state, and_6_out, and_7_out, and_8_out);

  // Notes on the sheet:
  //   Память
  //   Логика перехода
  //   Конечный автомат Мура (светофор)
endmodule
