// Digital circuit FSM2.dig as structural Verilog
module FSM2 (
  input  fsm_tick,
  output Q_0,
  output Q_1,
  output [7:0] out_counter,
  output change_of_state
);

  wire and_1_out, and_2_out, and_3_out, and_4_out, and_5_out, and_6_out, and_7_out, and_8_out, and_9_out,
       and_10_out, D0_q, D1_q, IF_0_gt, IF_1_gt, IF_2_gt, IF_3_gt, multiplexer_1_out, multiplexer_2_out,
       not_1_out, not_3_out, not_4_out, or_3_out, or_4_out, or_5_out, or_6_out;

  D_FF D0 (.D(multiplexer_1_out), .C(fsm_tick), .Q(D0_q));  // open: nQ
  D_FF D1 (.D(multiplexer_2_out), .C(fsm_tick), .Q(D1_q));  // open: nQ
  Multiplexer multiplexer_1 (.sel(change_of_state), .in_0(D0_q), .in_1(Q_0), .out(multiplexer_1_out));
  Multiplexer multiplexer_2 (.sel(change_of_state), .in_0(D1_q), .in_1(Q_1), .out(multiplexer_2_out));
  not not_1 (not_1_out, D0_q);
  not not_2 (Q_1, D1_q);
  CounterPreset #(.maxValue(255), .Bits(8)) counterpreset_1 (
    .en(1'b1), .C(fsm_tick), .dir(1'b0), .in({8{1'b0}}), .ld(change_of_state), .clr(change_of_state),
    .out(out_counter));  // open: ovf
  or or_1 (Q_0, and_1_out, and_2_out);
  and and_1 (and_1_out, not_1_out, D1_q);
  and and_2 (and_2_out, D0_q, Q_1);
  not not_3 (not_3_out, Q_0);
  not not_4 (not_4_out, Q_1);
  and and_3 (and_3_out, Q_0, Q_1);
  and and_4 (and_4_out, Q_0, not_4_out);
  and and_5 (and_5_out, Q_1, not_3_out);
  and and_6 (and_6_out, not_3_out, not_4_out);
  Comparator #(.Bits(8)) IF_2 (.a(out_counter), .b(8'ha), .gt(IF_2_gt));  // open: eq, lt
  Comparator #(.Bits(8)) IF_1 (.a(out_counter), .b(8'h3), .gt(IF_1_gt));  // open: eq, lt
  Comparator #(.Bits(8)) IF_0 (.a(out_counter), .b(8'h6), .gt(IF_0_gt));  // open: eq, lt
  Comparator #(.Bits(8)) IF_3 (.a(out_counter), .b(8'h6), .gt(IF_3_gt));  // open: eq, lt
  and and_7 (and_7_out, and_6_out, IF_2_gt);
  and and_8 (and_8_out, and_5_out, IF_1_gt);
  and and_9 (and_9_out, and_4_out, IF_0_gt);
  and and_10 (and_10_out, and_3_out, IF_3_gt);
  or or_2 (change_of_state, and_7_out, and_8_out, and_9_out, and_10_out);
  or or_3 (or_3_out, and_5_out, and_6_out);
  LED led_1 (.in(or_3_out));
  or or_4 (or_4_out, and_3_out, and_4_out);
  LED led_2 (.in(and_3_out));
  LED led_3 (.in(and_4_out));
  LED led_4 (.in(or_4_out));
  LED led_5 (.in(and_5_out));
  LED led_6 (.in(and_6_out));
  LED led_7 (.in(or_6_out));
  LED led_8 (.in(and_5_out));
  LED led_9 (.in(and_6_out));
  LED led_10 (.in(or_5_out));
  or or_5 (or_5_out, and_6_out, and_5_out);
  or or_6 (or_6_out, and_4_out, and_3_out);
  LED led_11 (.in(and_3_out));
  LED led_12 (.in(and_4_out));

  // Notes on the sheet:
  //   Память
  //   Логика перехода
  //   Конечный автомат Мура (светофор)
  //   S_3
  //   S_2
  //   S_1
  //   S_0
  //   .
  //   Дорога A
  //   Дорога B
endmodule
