// Digital circuit adder8bit_Kogge-Stone.dig as structural Verilog
module adder8bit_Kogge_Stone (
  input  cin_in,
  input  [7:0] b,
  input  [7:0] a,
  output [7:0] \output ,
  output cin_out
);

  wire and_1_out, and_2_out, and_3_out, and_4_out, and_5_out, and_6_out, and_7_out, and_8_out, and_9_out,
       and_10_out, and_11_out, and_12_out, and_13_out, and_14_out, and_15_out, and_16_out, and_17_out,
       and_18_out, and_19_out, and_20_out, and_21_out, and_22_out, and_23_out, and_24_out, and_25_out,
       and_26_out, and_27_out, and_28_out, and_29_out, and_30_out, and_31_out, and_32_out, and_33_out,
       and_34_out, and_35_out, and_36_out, or_1_out, or_2_out, or_4_out, or_5_out, or_6_out, or_7_out,
       or_8_out, or_9_out, or_10_out, or_11_out, or_12_out, or_13_out, or_14_out, or_15_out, or_16_out,
       or_17_out, or_18_out, xor_1_out, xor_4_out, xor_7_out, xor_11_out, xor_13_out, xor_14_out, xor_15_out,
       xor_16_out;

  and and_1 (and_1_out, b[7], a[7]);
  and and_2 (and_2_out, xor_1_out, and_7_out);
  or or_1 (or_1_out, and_2_out, and_1_out);
  or or_2 (or_2_out, and_4_out, or_1_out);
  xor xor_1 (xor_1_out, b[7], a[7]);
  and and_3 (and_3_out, xor_4_out, xor_1_out);
  and and_4 (and_4_out, and_3_out, or_7_out);
  and and_5 (and_5_out, and_16_out, and_3_out);
  and and_6 (and_6_out, and_5_out, or_14_out);
  or or_3 (cin_out, and_6_out, or_2_out);
  xor xor_2 (\output [7], or_6_out, xor_1_out);
  and and_7 (and_7_out, b[6], a[6]);
  and and_8 (and_8_out, xor_4_out, and_13_out);
  or or_4 (or_4_out, and_8_out, and_7_out);
  and and_9 (and_9_out, and_10_out, or_10_out);
  or or_5 (or_5_out, and_9_out, or_4_out);
  xor xor_3 (\output [6], or_9_out, xor_4_out);
  xor xor_4 (xor_4_out, b[6], a[6]);
  and and_10 (and_10_out, xor_7_out, xor_4_out);
  and and_11 (and_11_out, and_21_out, and_10_out);
  and and_12 (and_12_out, and_11_out, or_16_out);
  or or_6 (or_6_out, and_12_out, or_5_out);
  xor xor_5 (\output [5], or_12_out, xor_7_out);
  and and_13 (and_13_out, b[5], a[5]);
  xor xor_6 (\output [4], or_14_out, xor_11_out);
  xor xor_7 (xor_7_out, b[5], a[5]);
  and and_14 (and_14_out, xor_7_out, and_19_out);
  or or_7 (or_7_out, and_14_out, and_13_out);
  and and_15 (and_15_out, and_16_out, or_13_out);
  or or_8 (or_8_out, and_15_out, or_7_out);
  or or_9 (or_9_out, and_18_out, or_8_out);
  xor xor_8 (\output [3], or_16_out, xor_13_out);
  and and_16 (and_16_out, xor_11_out, xor_7_out);
  and and_17 (and_17_out, and_27_out, and_16_out);
  and and_18 (and_18_out, and_17_out, or_17_out);
  xor xor_9 (\output [2], or_17_out, xor_14_out);
  and and_19 (and_19_out, b[4], a[4]);
  or or_10 (or_10_out, and_20_out, and_19_out);
  xor xor_10 (\output [1], or_18_out, xor_15_out);
  xor xor_11 (xor_11_out, b[4], a[4]);
  and and_20 (and_20_out, xor_11_out, and_25_out);
  and and_21 (and_21_out, xor_13_out, xor_11_out);
  and and_22 (and_22_out, and_21_out, or_15_out);
  or or_11 (or_11_out, and_22_out, or_10_out);
  and and_23 (and_23_out, and_24_out, or_18_out);
  or or_12 (or_12_out, and_23_out, or_11_out);
  xor xor_12 (\output [0], cin_in, xor_16_out);
  and and_24 (and_24_out, and_32_out, and_21_out);
  and and_25 (and_25_out, b[3], a[3]);
  and and_26 (and_26_out, xor_13_out, and_29_out);
  or or_13 (or_13_out, and_26_out, and_25_out);
  or or_14 (or_14_out, and_28_out, or_13_out);
  xor xor_13 (xor_13_out, b[3], a[3]);
  and and_27 (and_27_out, xor_14_out, xor_13_out);
  and and_28 (and_28_out, and_27_out, or_17_out);
  and and_29 (and_29_out, b[2], a[2]);
  and and_30 (and_30_out, xor_14_out, and_33_out);
  or or_15 (or_15_out, and_30_out, and_29_out);
  and and_31 (and_31_out, and_32_out, or_18_out);
  or or_16 (or_16_out, and_31_out, or_15_out);
  xor xor_14 (xor_14_out, b[2], a[2]);
  and and_32 (and_32_out, xor_15_out, xor_14_out);
  and and_33 (and_33_out, b[1], a[1]);
  xor xor_15 (xor_15_out, b[1], a[1]);
  and and_34 (and_34_out, or_18_out, xor_15_out);
  or or_17 (or_17_out, and_34_out, and_33_out);
  and and_35 (and_35_out, b[0], a[0]);
  xor xor_16 (xor_16_out, b[0], a[0]);
  and and_36 (and_36_out, cin_in, xor_16_out);
  or or_18 (or_18_out, and_36_out, and_35_out);

  // Notes on the sheet:
  //   G_3
  //   G_2
  //   G_1
  //   G_0
  //   P_0
endmodule

/* Test case:
cin_in a b cin_out output
1 1 254 1 0
0 0 0 0 0
0 5 10 0 15
0 255 0 0 255
0 255 1 1 0
0 200 60 1 4
1 0 0 0 1
1 128 127 1 0
1 255 255 1 255
*/
