// Digital circuit bit_manipulation.dig as structural Verilog
module bit_manipulation (
  input  [2:0] c,
  input  [3:0] d,
  output [8:0] y
);

  bit_manipulation #(.applicationType("GHDL"), .CodeFile("/home/jeka/Projects/Rust/Computer-Science-Bookshelf/src/test_vhd/bit_manipulation.vhd")) u_bit_manipulation (
    .c(c), .d(d), .y(y));
endmodule

/* Test case:
c     d      y
0b000 0b0000 0b000000101
0b111 0b1111 0b111111101
0b101 0b0000 0b100001101
0b010 0b1111 0b011110101
0b110 0b0101 0b111110101
*/
