// Digital circuit fulladder.dig as structural Verilog
module fulladder (
  input  a,
  input  b,
  input  cin,
  output s,
  output cout
);

  fulladder #(.applicationType("GHDL"), .CodeFile("/home/jeka/Projects/Rust/Computer-Science-Bookshelf/src/test_vhd/fulladder.vhd")) u_fulladder (
    .a(a), .b(b), .cin(cin), .s(s), .cout(cout));
endmodule

/* Test case:
a b cin s cout
0 0 0   0 0
0 1 0   1 0
1 0 0   1 0
1 1 0   0 1
0 0 1   1 0
0 1 1   0 1
1 0 1   0 1
1 1 1   1 1
*/
