// Digital circuit gates.dig as structural Verilog
module gates (
  input  [3:0] a,
  input  [3:0] b,
  output [3:0] y2,
  output [3:0] y1,
  output [3:0] y4,
  output [3:0] y3,
  output [3:0] y5
);

  gates #(.applicationType("GHDL"), .CodeFile("/home/jeka/Projects/Rust/Computer-Science-Bookshelf/src/test_vhd/gates.vhd")) u_gates (
    .a(a), .b(b), .y1(y1), .y2(y2), .y3(y3), .y4(y4), .y5(y5));
endmodule

/* Test case gates:
a      b      y1     y2     y3     y4     y5
0b0000 0b0000 0b0000 0b0000 0b0000 0b1111 0b1111
0b1111 0b1111 0b1111 0b1111 0b0000 0b0000 0b0000
0b1010 0b0101 0b0000 0b1111 0b1111 0b1111 0b0000
0b1100 0b1010 0b1000 0b1110 0b0110 0b0111 0b0001
*/
