// Digital circuit inv.dig as structural Verilog
module inv (
  input  [3:0] a,
  output [3:0] y
);

  inv #(.applicationType("GHDL"), .CodeFile("/home/jeka/Projects/Rust/Computer-Science-Bookshelf/src/test_vhd/inv.vhd")) u_inv (
    .a(a), .y(y));
endmodule

/* Test case Test inv:
a    y
0b0000 0b1111
0b1111 0b0000
0b0101 0b1010
0b1010 0b0101
*/
