// Digital circuit mux4.dig as structural Verilog
module mux4 (
  input  [3:0] d0,
  input  [3:0] d1,
  input  [3:0] d2,
  input  [3:0] d3,
  input  [1:0] s,
  output [3:0] y
);

  mux4 #(.applicationType("GHDL"), .CodeFile("/home/jeka/Projects/Rust/Computer-Science-Bookshelf/src/test_vhd/mux4.vhd")) u_mux4 (
    .d0(d0), .d1(d1), .d2(d2), .d3(d3), .s(s), .y(y));
endmodule

/* Test case:
d0     d1     s   y
0b0000 0b1111 0   0b0000
0b0000 0b1111 1   0b1111
0b1010 0b0101 0   0b1010
0b1010 0b0101 1   0b0101
0b1100 0b0011 0   0b1100
0b1100 0b0011 1   0b0011
*/
