// Digital circuit ram_array.dig as structural Verilog
module ram_array (
  input  we,
  input  [5:0] adr,
  input  [31:0] din,
  input  clk,
  output [31:0] dout
);

  ram_array #(.applicationType("GHDL"), .CodeFile("/home/jeka/Projects/Rust/Computer-Science-Bookshelf/src/test_vhd/ram_array.vhd")) u_ram_array (
    .clk(clk), .we(we), .adr(adr), .din(din), .dout(dout));
endmodule

/* Test case:
clk we adr  din         dout
# После включения питания на выходе неизвестно что
0   0  0x00 0x00000000  X
# Записываем число 0xAAAA_BBBB по адресу 0x01
C   1  0x01 0xAAAABBBB  X
# Записываем число 0x1234_5678 по адресу 0x02
C   1  0x02 0x12345678  X
# Выключаем запись (we=0). Проверяем чтение адреса 0x01 (должно появиться немедленно)
0   0  0x01 0x00000000  0xAAAABBBB
# Переключаем адрес на 0x02 (чтение должно мгновенно измениться без тактового импульса)
0   0  0x02 0x00000000  0x12345678
# Проверяем, что по адресу 0x00 ничего не записалось
0   0  0x00 0x00000000  X
*/
