// Digital circuit alu.dig as structural Verilog
module alu (
  input  _2_addr,
  input  _1_addr,
  input  _0_addr,
  input  _7a_in,
  input  _6a_in,
  input  _5a_in,
  input  _4a_in,
  input  _3a_in,
  input  _2a_in,
  input  _1a_in,
  input  _0a_in,
  input  _7b_in,
  input  _6b_in,
  input  _5b_in,
  input  _4b_in,
  input  _3b_in,
  input  _2b_in,
  input  _1b_in,
  input  _0b_in,
  output carry_neg,
  output _7_out,
  output _6_out,
  output _5_out,
  output _4_out,
  output _3_out,
  output _2_out,
  output _1_out,
  output _0_out,
  output carry_sub,
  output carry_add
);

  wire dec_3_8_1__000, dec_3_8_1__001, dec_3_8_1__010, dec_3_8_1__011, dec_3_8_1__100, dec_3_8_1__101,
       full_adder_8bit_1__0_out, full_adder_8bit_1__1_out, full_adder_8bit_1__2_out,
       full_adder_8bit_1__3_out, full_adder_8bit_1__4_out, full_adder_8bit_1__5_out,
       full_adder_8bit_1__6_out, full_adder_8bit_1__7_out, full_adder_8bit_2__0_out,
       full_adder_8bit_2__1_out, full_adder_8bit_2__2_out, full_adder_8bit_2__3_out,
       full_adder_8bit_2__4_out, full_adder_8bit_2__5_out, full_adder_8bit_2__6_out,
       full_adder_8bit_2__7_out, nand_1_out, nand_2_out, nand_3_out, nand_4_out, nand_5_out, nand_6_out,
       nand_7_out, nand_8_out, nand_9_out, nand_10_out, nand_11_out, nand_12_out, nand_13_out, nand_14_out,
       nand_15_out, nand_16_out, neg_8bit_1__0_out, neg_8bit_1__1_out, neg_8bit_1__2_out, neg_8bit_1__3_out,
       neg_8bit_1__4_out, neg_8bit_1__5_out, neg_8bit_1__6_out, neg_8bit_1__7_out, not_1_out, not_2_out,
       not_3_out, not_4_out, not_5_out, not_6_out, not_7_out, not_8_out, not_9_out, not_10_out, not_11_out,
       not_12_out, not_13_out, not_14_out, not_15_out, not_16_out, not_17_out, not_18_out, not_19_out,
       not_20_out, not_21_out, not_22_out, not_23_out, not_24_out, not_25_out, not_26_out, not_27_out,
       not_28_out, not_29_out, not_30_out, not_31_out, not_32_out;

  dec_3_8 dec_3_8_1 (
    ._2_in(_2_addr), ._1_in(_1_addr), ._0_in(_0_addr), ._101(dec_3_8_1__101), ._100(dec_3_8_1__100),
    ._011(dec_3_8_1__011), ._010(dec_3_8_1__010), ._001(dec_3_8_1__001), ._000(dec_3_8_1__000));  // open: _111, _110
  neg_8bit neg_8bit_1 (
    ._7_in(_7b_in), ._6_in(_6b_in), ._5_in(_5b_in), ._4_in(_4b_in), ._3_in(_3b_in), ._2_in(_2b_in),
    ._1_in(_1b_in), ._0_in(_0b_in), .carry_out(carry_neg), ._7_out(neg_8bit_1__7_out),
    ._6_out(neg_8bit_1__6_out), ._5_out(neg_8bit_1__5_out), ._4_out(neg_8bit_1__4_out),
    ._3_out(neg_8bit_1__3_out), ._2_out(neg_8bit_1__2_out), ._1_out(neg_8bit_1__1_out),
    ._0_out(neg_8bit_1__0_out));
  full_adder_8bit full_adder_8bit_1 (
    ._7a_in(_7a_in), ._6a_in(_6a_in), ._5a_in(_5a_in), ._4a_in(_4a_in), ._3a_in(_3a_in), ._2a_in(_2a_in),
    ._1a_in(_1a_in), ._0a_in(_0a_in), ._7b_in(_7b_in), ._6b_in(_6b_in), ._5b_in(_5b_in), ._4b_in(_4b_in),
    ._3b_in(_3b_in), ._2b_in(_2b_in), ._1b_in(_1b_in), ._0b_in(_0b_in), .carry_in(1'b0),
    .carry_out(carry_add), ._7_out(full_adder_8bit_1__7_out), ._6_out(full_adder_8bit_1__6_out),
    ._5_out(full_adder_8bit_1__5_out), ._4_out(full_adder_8bit_1__4_out), ._3_out(full_adder_8bit_1__3_out),
    ._2_out(full_adder_8bit_1__2_out), ._1_out(full_adder_8bit_1__1_out), ._0_out(full_adder_8bit_1__0_out));
  nand nand_1 (nand_1_out, _7a_in, _7b_in);
  nand nand_2 (nand_2_out, _6a_in, _6b_in);
  nand nand_3 (nand_3_out, _5a_in, _5b_in);
  nand nand_4 (nand_4_out, _4a_in, _4b_in);
  nand nand_5 (nand_5_out, _3a_in, _3b_in);
  nand nand_6 (nand_6_out, _2a_in, _2b_in);
  nand nand_7 (nand_7_out, _1a_in, _1b_in);
  nand nand_8 (nand_8_out, _0a_in, _0b_in);
  not not_1 (not_1_out, _7a_in);
  not not_2 (not_2_out, _7b_in);
  not not_3 (not_3_out, _6a_in);
  not not_4 (not_4_out, _6b_in);
  not not_5 (not_5_out, _5a_in);
  not not_6 (not_6_out, _5b_in);
  not not_7 (not_7_out, _4a_in);
  not not_8 (not_8_out, _4b_in);
  not not_9 (not_9_out, _3a_in);
  not not_10 (not_10_out, _3b_in);
  not not_11 (not_11_out, _2a_in);
  not not_12 (not_12_out, _2b_in);
  not not_13 (not_13_out, _1a_in);
  not not_14 (not_14_out, _1b_in);
  not not_15 (not_15_out, _0a_in);
  not not_16 (not_16_out, _0b_in);
  nand nand_9 (nand_9_out, not_1_out, not_2_out);
  nand nand_10 (nand_10_out, not_3_out, not_4_out);
  nand nand_11 (nand_11_out, not_5_out, not_6_out);
  nand nand_12 (nand_12_out, not_7_out, not_8_out);
  nand nand_13 (nand_13_out, not_9_out, not_10_out);
  nand nand_14 (nand_14_out, not_11_out, not_12_out);
  nand nand_15 (nand_15_out, not_13_out, not_14_out);
  nand nand_16 (nand_16_out, not_15_out, not_16_out);
  full_adder_8bit full_adder_8bit_2 (
    ._7a_in(_7a_in), ._6a_in(_6a_in), ._5a_in(_5a_in), ._4a_in(_4a_in), ._3a_in(_3a_in), ._2a_in(_2a_in),
    ._1a_in(_1a_in), ._0a_in(_0a_in), ._7b_in(neg_8bit_1__7_out), ._6b_in(neg_8bit_1__6_out),
    ._5b_in(neg_8bit_1__5_out), ._4b_in(neg_8bit_1__4_out), ._3b_in(neg_8bit_1__3_out),
    ._2b_in(neg_8bit_1__2_out), ._1b_in(neg_8bit_1__1_out), ._0b_in(neg_8bit_1__0_out), .carry_in(1'b0),
    .carry_out(carry_sub), ._7_out(full_adder_8bit_2__7_out), ._6_out(full_adder_8bit_2__6_out),
    ._5_out(full_adder_8bit_2__5_out), ._4_out(full_adder_8bit_2__4_out), ._3_out(full_adder_8bit_2__3_out),
    ._2_out(full_adder_8bit_2__2_out), ._1_out(full_adder_8bit_2__1_out), ._0_out(full_adder_8bit_2__0_out));
  not not_17 (not_17_out, nand_1_out);
  not not_18 (not_18_out, nand_2_out);
  not not_19 (not_19_out, nand_3_out);
  not not_20 (not_20_out, nand_4_out);
  not not_21 (not_21_out, nand_5_out);
  not not_22 (not_22_out, nand_6_out);
  not not_23 (not_23_out, nand_7_out);
  not not_24 (not_24_out, nand_8_out);
  not not_25 (not_25_out, nand_9_out);
  not not_26 (not_26_out, nand_10_out);
  not not_27 (not_27_out, nand_11_out);
  not not_28 (not_28_out, nand_12_out);
  not not_29 (not_29_out, nand_13_out);
  not not_30 (not_30_out, nand_14_out);
  not not_31 (not_31_out, nand_15_out);
  not not_32 (not_32_out, nand_16_out);
  switch_8bit switch_8bit_1 (
    ._7_in(full_adder_8bit_2__7_out), ._6_in(full_adder_8bit_2__6_out), ._5_in(full_adder_8bit_2__5_out),
    ._4_in(full_adder_8bit_2__4_out), ._3_in(full_adder_8bit_2__3_out), ._2_in(full_adder_8bit_2__2_out),
    ._1_in(full_adder_8bit_2__1_out), ._0_in(full_adder_8bit_2__0_out), .sel(dec_3_8_1__101),
    ._7_out(_7_out), ._6_out(_6_out), ._5_out(_5_out), ._4_out(_4_out), ._3_out(_3_out), ._2_out(_2_out),
    ._1_out(_1_out), ._0_out(_0_out));
  switch_8bit switch_8bit_2 (
    ._7_in(full_adder_8bit_1__7_out), ._6_in(full_adder_8bit_1__6_out), ._5_in(full_adder_8bit_1__5_out),
    ._4_in(full_adder_8bit_1__4_out), ._3_in(full_adder_8bit_1__3_out), ._2_in(full_adder_8bit_1__2_out),
    ._1_in(full_adder_8bit_1__1_out), ._0_in(full_adder_8bit_1__0_out), .sel(dec_3_8_1__100),
    ._7_out(_7_out), ._6_out(_6_out), ._5_out(_5_out), ._4_out(_4_out), ._3_out(_3_out), ._2_out(_2_out),
    ._1_out(_1_out), ._0_out(_0_out));
  switch_8bit switch_8bit_3 (
    ._7_in(not_17_out), ._6_in(not_18_out), ._5_in(not_19_out), ._4_in(not_20_out), ._3_in(not_21_out),
    ._2_in(not_22_out), ._1_in(not_23_out), ._0_in(not_24_out), .sel(dec_3_8_1__011), ._7_out(_7_out),
    ._6_out(_6_out), ._5_out(_5_out), ._4_out(_4_out), ._3_out(_3_out), ._2_out(_2_out), ._1_out(_1_out),
    ._0_out(_0_out));
  switch_8bit switch_8bit_4 (
    ._7_in(nand_1_out), ._6_in(nand_2_out), ._5_in(nand_3_out), ._4_in(nand_4_out), ._3_in(nand_5_out),
    ._2_in(nand_6_out), ._1_in(nand_7_out), ._0_in(nand_8_out), .sel(dec_3_8_1__001), ._7_out(_7_out),
    ._6_out(_6_out), ._5_out(_5_out), ._4_out(_4_out), ._3_out(_3_out), ._2_out(_2_out), ._1_out(_1_out),
    ._0_out(_0_out));
  switch_8bit switch_8bit_5 (
    ._7_in(not_25_out), ._6_in(not_26_out), ._5_in(not_27_out), ._4_in(not_28_out), ._3_in(not_29_out),
    ._2_in(not_30_out), ._1_in(not_31_out), ._0_in(not_32_out), .sel(dec_3_8_1__010), ._7_out(_7_out),
    ._6_out(_6_out), ._5_out(_5_out), ._4_out(_4_out), ._3_out(_3_out), ._2_out(_2_out), ._1_out(_1_out),
    ._0_out(_0_out));
  switch_8bit switch_8bit_6 (
    ._7_in(nand_9_out), ._6_in(nand_10_out), ._5_in(nand_11_out), ._4_in(nand_12_out), ._3_in(nand_13_out),
    ._2_in(nand_14_out), ._1_in(nand_15_out), ._0_in(nand_16_out), .sel(dec_3_8_1__000), ._7_out(_7_out),
    ._6_out(_6_out), ._5_out(_5_out), ._4_out(_4_out), ._3_out(_3_out), ._2_out(_2_out), ._1_out(_1_out),
    ._0_out(_0_out));

  // Notes on the sheet:
  //   sub
  //   add
  //   and
  //   nor
  //   nand
  //   or
  //   Коротко что это значит:
  //   1. Arithmetic — сложение, вычитание, инкремент, декремент
  //   2. Logic — AND, OR, XOR, NOT, сравнения
  //   3. Unit — отдельный функциональный блок процессора
  //   NOR
  //   SUB
  //   ADD
  //   AND
  //   NAND
  //   OR
endmodule

/* Test case Arithmetic Logic Unit (ALU):
2_addr 1_addr 0_addr 7a_in 6a_in 5a_in 4a_in 3a_in 2a_in 1a_in 0a_in 7b_in 6b_in 5b_in 4b_in 3b_in 2b_in 1b_in 0b_in 7_out 6_out 5_out 4_out 3_out 2_out 1_out 0_out
0 0 0 0 0 0 0 0 0 0 0 0 0 0 0 0 0 0 0 0 0 0 0 0 0 0 0
0 0 0 0 0 0 0 0 0 0 0 1 1 1 1 1 1 1 1 1 1 1 1 1 1 1 1
0 0 0 0 1 0 1 0 1 0 1 1 0 1 0 1 0 1 0 1 1 1 1 1 1 1 1
0 0 0 1 1 1 1 1 1 1 1 1 1 1 1 1 1 1 1 1 1 1 1 1 1 1 1
0 0 1 0 0 0 0 0 0 0 0 0 0 0 0 0 0 0 0 1 1 1 1 1 1 1 1
0 0 1 1 1 1 1 1 1 1 1 1 1 1 1 1 1 1 1 0 0 0 0 0 0 0 0
0 0 1 0 1 0 1 0 1 0 1 1 0 1 0 1 0 1 0 1 1 1 1 1 1 1 1
0 0 1 1 1 1 1 1 1 1 1 0 0 0 0 0 0 0 0 1 1 1 1 1 1 1 1
0 1 0 0 0 0 0 0 0 0 0 0 0 0 0 0 0 0 0 1 1 1 1 1 1 1 1
0 1 0 0 0 0 0 0 0 0 0 1 1 1 1 1 1 1 1 0 0 0 0 0 0 0 0
0 1 0 0 1 0 1 0 1 0 1 1 0 1 0 1 0 1 0 0 0 0 0 0 0 0 0
0 1 0 1 1 1 1 1 1 1 1 1 1 1 1 1 1 1 1 0 0 0 0 0 0 0 0
0 1 1 0 0 0 0 0 0 0 0 0 0 0 0 0 0 0 0 0 0 0 0 0 0 0 0
0 1 1 1 1 1 1 1 1 1 1 1 1 1 1 1 1 1 1 1 1 1 1 1 1 1 1
0 1 1 0 1 0 1 0 1 0 1 1 0 1 0 1 0 1 0 0 0 0 0 0 0 0 0
0 1 1 1 1 1 1 0 0 0 0 0 0 0 0 1 1 1 1 0 0 0 0 0 0 0 0
0 1 1 1 1 1 1 1 1 1 1 0 0 0 0 0 0 0 1 0 0 0 0 0 0 0 1
1 0 0 0 0 0 0 0 0 0 0 0 0 0 0 0 0 0 0 0 0 0 0 0 0 0 0
1 0 0 0 0 0 0 0 0 0 1 0 0 0 0 0 0 0 1 0 0 0 0 0 0 1 0
1 0 0 0 1 1 1 1 1 1 1 0 0 0 0 0 0 0 1 1 0 0 0 0 0 0 0
1 0 0 1 1 1 1 1 1 1 1 0 0 0 0 0 0 0 1 0 0 0 0 0 0 0 0
1 0 0 0 1 0 1 0 1 0 1 1 0 1 0 1 0 1 0 1 1 1 1 1 1 1 1
1 0 0 1 0 0 0 0 0 0 0 1 0 0 0 0 0 0 0 0 0 0 0 0 0 0 0
1 0 1 0 0 0 0 0 0 0 0 0 0 0 0 0 0 0 0 0 0 0 0 0 0 0 0
1 0 1 0 0 0 0 0 1 0 1 0 0 0 0 0 0 1 1 0 0 0 0 0 0 1 0
1 0 1 0 0 0 0 0 0 0 0 0 0 0 0 0 0 0 1 1 1 1 1 1 1 1 1
1 0 1 1 0 0 0 0 0 0 0 1 0 0 0 0 0 0 0 0 0 0 0 0 0 0 0
1 0 1 1 1 1 1 1 1 1 1 1 1 1 1 1 1 1 0 0 0 0 0 0 0 0 1
1 0 1 0 1 1 0 0 1 0 0 1 1 0 0 1 0 0 0 1 0 0 1 1 1 0 0
0 0 0 1 0 1 0 1 0 1 0 0 1 0 1 0 1 0 1 1 1 1 1 1 1 1 1
0 1 1 1 1 0 0 1 1 0 0 0 0 1 1 0 0 1 1 0 0 0 0 0 0 0 0
1 0 0 1 1 1 1 1 1 1 1 1 1 1 1 1 1 1 1 1 1 1 1 1 1 1 0
1 0 1 0 0 0 0 0 0 0 1 1 1 1 1 1 1 1 1 0 0 0 0 0 0 1 0
0 0 0 0 0 0 0 0 0 0 0 0 0 0 0 0 0 0 0 0 0 0 0 0 0 0 0
0 1 1 1 1 1 1 1 1 1 1 1 1 1 1 1 1 1 1 1 1 1 1 1 1 1 1
1 0 0 1 1 1 1 1 1 1 1 0 0 0 0 0 0 0 0 1 1 1 1 1 1 1 1
1 0 1 1 1 1 1 1 1 1 1 1 1 1 1 1 1 1 1 0 0 0 0 0 0 0 0
*/
