// Digital circuit conditions.dig as structural Verilog
module conditions (
  input  _2_addr,
  input  _1_addr,
  input  _0_addr,
  input  _7_in,
  input  _6_in,
  input  _5_in,
  input  _4_in,
  input  _3_in,
  input  _2_in,
  input  _1_in,
  input  _0_in,
  output out
);

  wire dec_3_8_1__001, dec_3_8_1__010, dec_3_8_1__011, dec_3_8_1__100, dec_3_8_1__101, dec_3_8_1__110,
       dec_3_8_1__111, nor_1_out, nor_2_out, not_1_out, not_2_out, or_1_out, or_2_out, or_3_out, or_4_out;

  dec_3_8 dec_3_8_1 (
    ._2_in(_2_addr), ._1_in(_1_addr), ._0_in(_0_addr), ._111(dec_3_8_1__111), ._110(dec_3_8_1__110),
    ._101(dec_3_8_1__101), ._100(dec_3_8_1__100), ._011(dec_3_8_1__011), ._010(dec_3_8_1__010),
    ._001(dec_3_8_1__001));  // open: _000
  or or_1 (or_1_out, _6_in, _5_in, _4_in);
  or or_2 (or_2_out, _2_in, _1_in, _0_in);
  or or_3 (or_3_out, or_1_out, _3_in, or_2_out);
  nor nor_1 (nor_1_out, _7_in, or_3_out);
  or or_4 (or_4_out, nor_1_out, _7_in);
  nor nor_2 (nor_2_out, _7_in, nor_1_out);
  not not_1 (not_1_out, nor_1_out);
  not not_2 (not_2_out, _7_in);
  assign out = dec_3_8_1__001 ? nor_1_out : 1'bz;  // Driver driver_1
  assign out = dec_3_8_1__010 ? _7_in : 1'bz;  // Driver driver_2
  assign out = dec_3_8_1__011 ? or_4_out : 1'bz;  // Driver driver_3
  assign out = dec_3_8_1__100 ? dec_3_8_1__100 : 1'bz;  // Driver driver_4
  assign out = dec_3_8_1__101 ? not_1_out : 1'bz;  // Driver driver_5
  assign out = dec_3_8_1__110 ? not_2_out : 1'bz;  // Driver driver_6
  assign out = dec_3_8_1__111 ? nor_2_out : 1'bz;  // Driver driver_7

  // Notes on the sheet:
  //   Conditions
  //   Data
  //   000 never
  //   001 == 0
  //   010 < 0
  //   011 ≤ 0
  //   100 always
  //   101 != 0
  //   110 ≥ 0
  //   111 > 0
  //   == 0
  //   <   0
  //   <= 0
  //   == 1
  //   != 0
  //   >= 0
  //   >  0
endmodule

/* Test case Conditions:
2_addr 1_addr 0_addr 7_in 6_in 5_in 4_in 3_in 2_in 1_in 0_in out
0 0 0 0 0 0 0 0 0 0 0 Z
0 0 1 0 0 0 0 0 0 0 0 1
0 1 0 1 0 0 0 0 0 0 0 1
0 1 1 1 0 0 0 0 0 0 0 1
1 0 0 0 0 0 0 0 0 0 0 1
1 0 1 0 0 0 0 0 0 0 0 0
1 1 0 0 0 0 0 0 0 0 1 1
1 1 1 0 0 0 0 0 0 0 1 1
*/
