// Digital circuit d_trigger_falling_sync.dig as structural Verilog
module d_trigger_falling_sync (
  input  data,
  input  clk,
  input  reset,
  output Q,
  output Q_2
);

  wire nand_1_out, nand_2_out, nand_3_out, nand_4_out, nand_5_out, nand_6_out, not_1_out;

  nand nand_1 (nand_1_out, data, clk);
  nand nand_2 (nand_2_out, nand_1_out, clk);
  not not_1 (not_1_out, clk);
  nand nand_3 (nand_3_out, nand_4_out, nand_2_out, reset);
  nand nand_4 (nand_4_out, nand_1_out, nand_3_out);
  nand nand_5 (nand_5_out, nand_4_out, not_1_out);
  nand nand_6 (nand_6_out, not_1_out, nand_3_out);
  nand nand_7 (Q_2, Q, reset, nand_6_out);
  nand nand_8 (Q, nand_5_out, Q_2);

  // Notes on the sheet:
  //   Устойчивое начальное состояние симуляции Q=LOW, !Q=HIGH обеспечивает input resert=LOW по умолчанию
  //   Master gated D Latch
  //   Synchronous reset. Active LOW level
  //   Slave gates SR Latch
endmodule

/* Test case D-Trigger falling edge. Synchronous reset LOW level:
data clk reset Q !Q
0 0 0 0 1
0 1 1 0 1
1 1 1 0 1
1 0 1 1 0
1 0 0 0 1
*/
