// Digital circuit d_trigger_rising_async.dig as structural Verilog
module d_trigger_rising_async (
  input  set,
  input  clk,
  input  reset,
  input  data,
  output Q,
  output Q_2
);

  wire nand_1_out, nand_2_out, nand_3_out, nand_4_out;

  nand nand_1 (nand_1_out, set, nand_4_out, nand_2_out);
  nand nand_2 (nand_2_out, nand_1_out, reset, clk);
  nand nand_3 (nand_3_out, clk, nand_2_out, nand_4_out);
  nand nand_4 (nand_4_out, nand_3_out, data, reset);
  nand nand_5 (Q, set, nand_2_out, Q_2);
  nand nand_6 (Q_2, Q, nand_3_out, reset);

  // Notes on the sheet:
  //   set: default 1
  //   Устойчивое начальное состояние симуляции Q=LOW, !Q=HIGH обеспечивает input set=HIGH и resert=LOW по умолчанию
  //   Asynchronous set and reset. Active LOW level
endmodule

/* Test case D-trigger rising edge. Asynchronous set and reset LOW level:
set clk data reset Q !Q
0 0 0 1 1 0
0 0 0 0 1 1
1 0 0 0 0 1
1 0 0 1 0 1
1 0 1 1 0 1
1 1 1 1 1 0
1 0 1 1 1 0
1 0 0 1 1 0
1 1 0 1 0 1
1 1 1 1 0 1
1 0 1 1 0 1
1 1 1 1 1 0
*/
