// Digital circuit dec_2_4.dig as structural Verilog
module dec_2_4 (
  input  _1_in,
  input  _0_in,
  output _11,
  output _10,
  output _01,
  output _00
);

  wire not_1_out, not_2_out;

  not not_1 (not_1_out, _1_in);
  not not_2 (not_2_out, _0_in);
  and and_1 (_11, _1_in, _0_in);
  and and_2 (_10, _1_in, not_2_out);
  and and_3 (_01, not_1_out, _0_in);
  and and_4 (_00, not_1_out, not_2_out);
endmodule

/* Test case Decoder 2 to 4:
1_in 0_in 11 10 01 00
0 0 0 0 0 1
0 1 0 0 1 0
1 0 0 1 0 0
1 1 1 0 0 0
*/
