// Digital circuit dec_3_8.dig as structural Verilog
module dec_3_8 (
  input  _2_in,
  input  _1_in,
  input  _0_in,
  output _111,
  output _110,
  output _101,
  output _100,
  output _011,
  output _010,
  output _001,
  output _000
);

  wire not_1_out, not_2_out, not_3_out;

  not not_1 (not_1_out, _2_in);
  not not_2 (not_2_out, _1_in);
  not not_3 (not_3_out, _0_in);
  and and_1 (_111, _2_in, _1_in, _0_in);
  and and_2 (_110, _2_in, _1_in, not_3_out);
  and and_3 (_101, _2_in, not_2_out, _0_in);
  and and_4 (_100, _2_in, not_2_out, not_3_out);
  and and_5 (_011, not_1_out, _1_in, _0_in);
  and and_6 (_010, not_1_out, _1_in, not_3_out);
  and and_7 (_001, not_1_out, not_2_out, _0_in);
  and and_8 (_000, not_1_out, not_2_out, not_3_out);
endmodule

/* Test case Decoder 3 to 8:
2_in 1_in 0_in 111 110 101 100 011 010 001 000
0 0 0 0 0 0 0 0 0 0 1
0 0 1 0 0 0 0 0 0 1 0
0 1 0 0 0 0 0 0 1 0 0
0 1 1 0 0 0 0 1 0 0 0
1 0 0 0 0 0 1 0 0 0 0
1 0 1 0 0 1 0 0 0 0 0
1 1 0 0 1 0 0 0 0 0 0
1 1 1 1 0 0 0 0 0 0 0
*/
