// Digital circuit dec_3_8_disable.dig as structural Verilog
module dec_3_8_disable (
  input  _2_in,
  input  _1_in,
  input  _0_in,
  input  sel,
  output _111,
  output _110,
  output _101,
  output _100,
  output _011,
  output _010,
  output _001,
  output _000
);

  wire and_1_out, and_2_out, and_3_out, and_4_out, and_5_out, and_6_out, and_7_out, and_8_out, not_1_out,
       not_2_out, not_3_out;

  not not_1 (not_1_out, _2_in);
  not not_2 (not_2_out, _1_in);
  not not_3 (not_3_out, _0_in);
  and and_1 (and_1_out, _2_in, _1_in, _0_in);
  and and_2 (and_2_out, _2_in, _1_in, not_3_out);
  and and_3 (and_3_out, _2_in, not_2_out, _0_in);
  and and_4 (and_4_out, _2_in, not_2_out, not_3_out);
  and and_5 (and_5_out, not_1_out, _1_in, _0_in);
  and and_6 (and_6_out, not_1_out, _1_in, not_3_out);
  and and_7 (and_7_out, not_1_out, not_2_out, _0_in);
  and and_8 (and_8_out, not_1_out, not_2_out, not_3_out);
  mux_8bit mux_8bit_1 (
    .sel(sel), ._7a_in(1'b0), ._6a_in(1'b0), ._5a_in(1'b0), ._4a_in(1'b0), ._3a_in(1'b0), ._2a_in(1'b0),
    ._1a_in(1'b0), ._0a_in(1'b0), ._7b_in(and_1_out), ._6b_in(and_2_out), ._5b_in(and_3_out),
    ._4b_in(and_4_out), ._3b_in(and_5_out), ._2b_in(and_6_out), ._1b_in(and_7_out), ._0b_in(and_8_out),
    ._7_out(_111), ._6_out(_110), ._5_out(_101), ._4_out(_100), ._3_out(_011), ._2_out(_010), ._1_out(_001),
    ._0_out(_000));
endmodule

/* Test case Decoder 3 to 8. Disable sel=0:
sel 2_in 1_in 0_in 111 110 101 100 011 010 001 000
1 0 0 0 0 0 0 0 0 0 0 1
1 0 0 1 0 0 0 0 0 0 1 0
1 0 1 0 0 0 0 0 0 1 0 0
1 0 1 1 0 0 0 0 1 0 0 0
1 1 0 0 0 0 0 1 0 0 0 0
1 1 0 1 0 0 1 0 0 0 0 0
1 1 1 0 0 1 0 0 0 0 0 0
1 1 1 1 1 0 0 0 0 0 0 0
0 0 0 0 0 0 0 0 0 0 0 0
0 1 1 1 0 0 0 0 0 0 0 0
*/
