// Digital circuit full_adder_1bit.dig as structural Verilog
module full_adder_1bit (
  input  a_in,
  input  b_in,
  input  carry_in,
  output carry_out,
  output sum_out
);

  wire and_1_out, and_2_out, xor_1_out;

  xor xor_1 (xor_1_out, a_in, b_in);
  and and_1 (and_1_out, a_in, b_in);
  and and_2 (and_2_out, xor_1_out, carry_in);
  xor xor_2 (sum_out, xor_1_out, carry_in);
  or or_1 (carry_out, and_2_out, and_1_out);
endmodule

/* Test case Full Adder:
a_in b_in carry_in carry_out sum_out
0 0 0 0 0
0 0 1 0 1
1 0 1 1 0
0 1 1 1 0
1 1 0 1 0
1 1 1 1 1
*/
