// Digital circuit full_adder_8bit.dig as structural Verilog
module full_adder_8bit (
  input  _7a_in,
  input  _6a_in,
  input  _5a_in,
  input  _4a_in,
  input  _3a_in,
  input  _2a_in,
  input  _1a_in,
  input  _0a_in,
  input  _7b_in,
  input  _6b_in,
  input  _5b_in,
  input  _4b_in,
  input  _3b_in,
  input  _2b_in,
  input  _1b_in,
  input  _0b_in,
  input  carry_in,
  output carry_out,
  output _7_out,
  output _6_out,
  output _5_out,
  output _4_out,
  output _3_out,
  output _2_out,
  output _1_out,
  output _0_out
);

  wire full_adder_1bit_1_carry_out, full_adder_1bit_2_carry_out, full_adder_1bit_3_carry_out,
       full_adder_1bit_4_carry_out, full_adder_1bit_5_carry_out, full_adder_1bit_6_carry_out,
       full_adder_1bit_7_carry_out;

  full_adder_1bit full_adder_1bit_1 (
    .a_in(_0a_in), .b_in(_0b_in), .carry_in(carry_in), .carry_out(full_adder_1bit_1_carry_out),
    .sum_out(_0_out));
  full_adder_1bit full_adder_1bit_2 (
    .a_in(_1a_in), .b_in(_1b_in), .carry_in(full_adder_1bit_1_carry_out),
    .carry_out(full_adder_1bit_2_carry_out), .sum_out(_1_out));
  full_adder_1bit full_adder_1bit_3 (
    .a_in(_2a_in), .b_in(_2b_in), .carry_in(full_adder_1bit_2_carry_out),
    .carry_out(full_adder_1bit_3_carry_out), .sum_out(_2_out));
  full_adder_1bit full_adder_1bit_4 (
    .a_in(_3a_in), .b_in(_3b_in), .carry_in(full_adder_1bit_3_carry_out),
    .carry_out(full_adder_1bit_4_carry_out), .sum_out(_3_out));
  full_adder_1bit full_adder_1bit_5 (
    .a_in(_4a_in), .b_in(_4b_in), .carry_in(full_adder_1bit_4_carry_out),
    .carry_out(full_adder_1bit_5_carry_out), .sum_out(_4_out));
  full_adder_1bit full_adder_1bit_6 (
    .a_in(_5a_in), .b_in(_5b_in), .carry_in(full_adder_1bit_5_carry_out),
    .carry_out(full_adder_1bit_6_carry_out), .sum_out(_5_out));
  full_adder_1bit full_adder_1bit_7 (
    .a_in(_6a_in), .b_in(_6b_in), .carry_in(full_adder_1bit_6_carry_out),
    .carry_out(full_adder_1bit_7_carry_out), .sum_out(_6_out));
  full_adder_1bit full_adder_1bit_8 (
    .a_in(_7a_in), .b_in(_7b_in), .carry_in(full_adder_1bit_7_carry_out), .carry_out(carry_out),
    .sum_out(_7_out));
endmodule

/* Test case Full Adder 8 bit:
7a_in 6a_in 5a_in 4a_in 3a_in 2a_in 1a_in 0a_in 7b_in 6b_in 5b_in 4b_in 3b_in 2b_in 1b_in 0b_in carry_in carry_out 7_out 6_out 5_out 4_out 3_out 2_out 1_out 0_out
0 0 0 0 0 0 0 0 0 0 0 0 0 0 0 0 0 0 0 0 0 0 0 0 0 0
0 0 0 0 0 0 0 0 0 0 0 0 0 0 0 0 1 0 0 0 0 0 0 0 0 1
1 1 1 1 1 1 1 1 0 0 0 0 0 0 0 0 0 0 1 1 1 1 1 1 1 1
1 1 1 1 1 1 1 1 0 0 0 0 0 0 0 0 1 1 0 0 0 0 0 0 0 0
1 1 1 1 1 1 1 1 0 0 0 0 0 0 0 1 0 1 0 0 0 0 0 0 0 0
1 1 1 1 1 1 1 1 1 1 1 1 1 1 1 1 0 1 1 1 1 1 1 1 1 0
1 1 1 1 1 1 1 1 1 1 1 1 1 1 1 1 1 1 1 1 1 1 1 1 1 1
1 0 1 0 1 0 1 0 0 1 0 1 0 1 0 1 0 0 1 1 1 1 1 1 1 1
1 0 1 0 1 0 1 0 0 1 0 1 0 1 0 1 1 1 0 0 0 0 0 0 0 0
1 0 0 0 0 0 0 0 1 0 0 0 0 0 0 0 0 1 0 0 0 0 0 0 0 0
0 1 0 0 0 0 0 0 0 1 0 0 0 0 0 0 0 0 1 0 0 0 0 0 0 0
0 0 0 0 0 0 0 1 1 1 1 1 1 1 1 1 0 1 0 0 0 0 0 0 0 0
0 0 0 0 1 1 1 1 1 1 1 1 0 0 0 0 0 0 1 1 1 1 1 1 1 1
0 0 1 0 1 0 1 0 0 1 0 0 1 0 0 1 0 0 0 1 1 1 0 0 1 1
0 0 1 0 1 0 1 0 0 1 0 0 1 0 0 1 1 0 0 1 1 1 0 1 0 0
0 1 1 1 1 0 1 1 1 1 1 0 0 1 1 1 0 1 0 1 1 0 0 0 1 0
1 0 1 1 1 0 1 1 0 1 0 0 0 1 0 0 1 1 0 0 0 0 0 0 0 0
*/
