// Digital circuit mux_1bit.dig as structural Verilog
module mux_1bit (
  input  sel,
  input  _0_in,
  input  _1_in,
  output Q
);

  wire and_1_out, and_2_out, not_1_out;

  not not_1 (not_1_out, sel);
  and and_1 (and_1_out, not_1_out, _0_in);
  and and_2 (and_2_out, sel, _1_in);
  or or_1 (Q, and_1_out, and_2_out);
endmodule

/* Test case Multuplexers 1 bit (MUX):
sel 0_in 1_in Q
0 1 0 1
0 0 1 0
0 0 0 0
1 0 1 1
1 1 1 1
1 1 0 0
*/
