// Digital circuit mux_8bit.dig as structural Verilog
module mux_8bit (
  input  sel,
  input  _7a_in,
  input  _6a_in,
  input  _5a_in,
  input  _4a_in,
  input  _3a_in,
  input  _2a_in,
  input  _1a_in,
  input  _0a_in,
  input  _7b_in,
  input  _6b_in,
  input  _5b_in,
  input  _4b_in,
  input  _3b_in,
  input  _2b_in,
  input  _1b_in,
  input  _0b_in,
  output _7_out,
  output _6_out,
  output _5_out,
  output _4_out,
  output _3_out,
  output _2_out,
  output _1_out,
  output _0_out
);

  mux_1bit mux_1bit_1 (.sel(sel), ._0_in(_7a_in), ._1_in(_7b_in), .Q(_7_out));
  mux_1bit mux_1bit_2 (.sel(sel), ._0_in(_6a_in), ._1_in(_6b_in), .Q(_6_out));
  mux_1bit mux_1bit_3 (.sel(sel), ._0_in(_5a_in), ._1_in(_5b_in), .Q(_5_out));
  mux_1bit mux_1bit_4 (.sel(sel), ._0_in(_4a_in), ._1_in(_4b_in), .Q(_4_out));
  mux_1bit mux_1bit_5 (.sel(sel), ._0_in(_3a_in), ._1_in(_3b_in), .Q(_3_out));
  mux_1bit mux_1bit_6 (.sel(sel), ._0_in(_2a_in), ._1_in(_2b_in), .Q(_2_out));
  mux_1bit mux_1bit_7 (.sel(sel), ._0_in(_1a_in), ._1_in(_1b_in), .Q(_1_out));
  mux_1bit mux_1bit_8 (.sel(sel), ._0_in(_0a_in), ._1_in(_0b_in), .Q(_0_out));
endmodule

/* Test case Multuplexers 8 bit (MUX):
sel 7a_in 6a_in 5a_in 4a_in 3a_in 2a_in 1a_in 0a_in 7b_in 6b_in 5b_in 4b_in 3b_in 2b_in 1b_in 0b_in 7_out 6_out 5_out 4_out 3_out 2_out 1_out 0_out 
0 1 1 1 1 1 1 1 1 1 1 1 1 1 1 1 1 1 1 1 1 1 1 1 1
0 0 0 0 0 0 0 0 0 1 1 1 1 1 1 1 1 0 0 0 0 0 0 0 0
0 0 0 0 0 0 0 0 0 0 0 0 0 0 0 0 0 0 0 0 0 0 0 0 0
1 0 0 0 0 0 0 0 0 1 1 1 1 1 1 1 1 1 1 1 1 1 1 1 1
1 1 1 1 1 1 1 1 1 1 1 1 1 1 1 1 1 1 1 1 1 1 1 1 1
1 1 1 1 1 1 1 1 1 0 0 0 0 0 0 0 0 0 0 0 0 0 0 0 0
*/
