// Digital circuit mux_8bit_Z.dig as structural Verilog
module mux_8bit_Z (
  input  sel,
  input  _7a_in,
  input  _6a_in,
  input  _5a_in,
  input  _4a_in,
  input  _3a_in,
  input  _2a_in,
  input  _1a_in,
  input  _0a_in,
  input  _7b_in,
  input  _6b_in,
  input  _5b_in,
  input  _4b_in,
  input  _3b_in,
  input  _2b_in,
  input  _1b_in,
  input  _0b_in,
  output _7_out,
  output _6_out,
  output _5_out,
  output _4_out,
  output _3_out,
  output _2_out,
  output _1_out,
  output _0_out
);

  wire not_1_out, or_1_out;

  or or_1 (or_1_out, sel, 1'b0);
  not not_1 (not_1_out, or_1_out);
  assign _7_out = not_1_out ? _7a_in : 1'bz;  // Driver driver_1
  assign _6_out = not_1_out ? _6a_in : 1'bz;  // Driver driver_2
  assign _5_out = not_1_out ? _5a_in : 1'bz;  // Driver driver_3
  assign _4_out = not_1_out ? _4a_in : 1'bz;  // Driver driver_4
  assign _3_out = not_1_out ? _3a_in : 1'bz;  // Driver driver_5
  assign _2_out = not_1_out ? _2a_in : 1'bz;  // Driver driver_6
  assign _1_out = not_1_out ? _1a_in : 1'bz;  // Driver driver_7
  assign _0_out = not_1_out ? _0a_in : 1'bz;  // Driver driver_8
  assign _7_out = or_1_out ? _7b_in : 1'bz;  // Driver driver_9
  assign _6_out = or_1_out ? _6b_in : 1'bz;  // Driver driver_10
  assign _5_out = or_1_out ? _5b_in : 1'bz;  // Driver driver_11
  assign _4_out = or_1_out ? _4b_in : 1'bz;  // Driver driver_12
  assign _3_out = or_1_out ? _3b_in : 1'bz;  // Driver driver_13
  assign _2_out = or_1_out ? _2b_in : 1'bz;  // Driver driver_14
  assign _1_out = or_1_out ? _1b_in : 1'bz;  // Driver driver_15
  assign _0_out = or_1_out ? _0b_in : 1'bz;  // Driver driver_16
endmodule

/* Test case Multuplexers 8 bit (MUX) with tri-state buffer:
sel 7a_in 6a_in 5a_in 4a_in 3a_in 2a_in 1a_in 0a_in 7b_in 6b_in 5b_in 4b_in 3b_in 2b_in 1b_in 0b_in 7_out 6_out 5_out 4_out 3_out 2_out 1_out 0_out 
0 1 1 1 1 1 1 1 1 1 1 1 1 1 1 1 1 1 1 1 1 1 1 1 1
0 0 0 0 0 0 0 0 0 1 1 1 1 1 1 1 1 0 0 0 0 0 0 0 0
0 0 0 0 0 0 0 0 0 0 0 0 0 0 0 0 0 0 0 0 0 0 0 0 0
1 0 0 0 0 0 0 0 0 1 1 1 1 1 1 1 1 1 1 1 1 1 1 1 1
1 1 1 1 1 1 1 1 1 1 1 1 1 1 1 1 1 1 1 1 1 1 1 1 1
1 1 1 1 1 1 1 1 1 0 0 0 0 0 0 0 0 0 0 0 0 0 0 0 0
*/
