// Digital circuit neg_8bit.dig as structural Verilog
module neg_8bit (
  input  _7_in,
  input  _6_in,
  input  _5_in,
  input  _4_in,
  input  _3_in,
  input  _2_in,
  input  _1_in,
  input  _0_in,
  output carry_out,
  output _7_out,
  output _6_out,
  output _5_out,
  output _4_out,
  output _3_out,
  output _2_out,
  output _1_out,
  output _0_out
);

  wire full_adder_1bit_1_carry_out, full_adder_1bit_2_carry_out, full_adder_1bit_3_carry_out,
       full_adder_1bit_4_carry_out, full_adder_1bit_5_carry_out, full_adder_1bit_6_carry_out,
       full_adder_1bit_7_carry_out, not_1_out, not_2_out, not_3_out, not_4_out, not_5_out, not_6_out,
       not_7_out, not_8_out;

  not not_1 (not_1_out, _0_in);
  full_adder_1bit full_adder_1bit_1 (
    .a_in(not_1_out), .b_in(1'b1), .carry_in(1'b0), .carry_out(full_adder_1bit_1_carry_out), .sum_out(_0_out));
  not not_2 (not_2_out, _1_in);
  full_adder_1bit full_adder_1bit_2 (
    .a_in(not_2_out), .b_in(1'b0), .carry_in(full_adder_1bit_1_carry_out),
    .carry_out(full_adder_1bit_2_carry_out), .sum_out(_1_out));
  not not_3 (not_3_out, _2_in);
  full_adder_1bit full_adder_1bit_3 (
    .a_in(not_3_out), .b_in(1'b0), .carry_in(full_adder_1bit_2_carry_out),
    .carry_out(full_adder_1bit_3_carry_out), .sum_out(_2_out));
  not not_4 (not_4_out, _3_in);
  full_adder_1bit full_adder_1bit_4 (
    .a_in(not_4_out), .b_in(1'b0), .carry_in(full_adder_1bit_3_carry_out),
    .carry_out(full_adder_1bit_4_carry_out), .sum_out(_3_out));
  not not_5 (not_5_out, _4_in);
  full_adder_1bit full_adder_1bit_5 (
    .a_in(not_5_out), .b_in(1'b0), .carry_in(full_adder_1bit_4_carry_out),
    .carry_out(full_adder_1bit_5_carry_out), .sum_out(_4_out));
  not not_6 (not_6_out, _5_in);
  full_adder_1bit full_adder_1bit_6 (
    .a_in(not_6_out), .b_in(1'b0), .carry_in(full_adder_1bit_5_carry_out),
    .carry_out(full_adder_1bit_6_carry_out), .sum_out(_5_out));
  not not_7 (not_7_out, _6_in);
  full_adder_1bit full_adder_1bit_7 (
    .a_in(not_7_out), .b_in(1'b0), .carry_in(full_adder_1bit_6_carry_out),
    .carry_out(full_adder_1bit_7_carry_out), .sum_out(_6_out));
  not not_8 (not_8_out, _7_in);
  full_adder_1bit full_adder_1bit_8 (
    .a_in(not_8_out), .b_in(1'b0), .carry_in(full_adder_1bit_7_carry_out), .carry_out(carry_out),
    .sum_out(_7_out));
endmodule

/* Test case NEG 8 bit:
7_in 6_in 5_in 4_in 3_in 2_in 1_in 0_in carry_out 7_out 6_out 5_out 4_out 3_out 2_out 1_out 0_out
0 0 0 0 0 0 0 0 1 0 0 0 0 0 0 0 0
0 0 0 0 0 0 0 1 0 1 1 1 1 1 1 1 1
1 1 1 1 1 1 1 1 0 0 0 0 0 0 0 0 1
0 1 1 1 1 1 1 1 0 1 0 0 0 0 0 0 1
1 0 0 0 0 0 0 0 0 1 0 0 0 0 0 0 0
0 1 0 0 0 0 0 0 0 1 1 0 0 0 0 0 0
0 0 1 0 0 0 0 0 0 1 1 1 0 0 0 0 0
0 0 0 1 0 0 0 0 0 1 1 1 1 0 0 0 0
0 0 0 0 1 0 0 0 0 1 1 1 1 1 0 0 0
0 0 0 0 0 1 0 0 0 1 1 1 1 1 1 0 0
0 0 0 0 0 0 1 0 0 1 1 1 1 1 1 1 0
0 1 0 1 0 1 0 1 0 1 0 1 0 1 0 1 1
1 0 1 0 1 0 1 0 0 0 1 0 1 0 1 1 0
0 0 0 0 1 1 1 1 0 1 1 1 1 0 0 0 1
1 1 1 1 0 0 0 0 0 0 0 0 1 0 0 0 0
0 0 1 0 1 0 1 0 0 1 1 0 1 0 1 1 0
0 1 0 0 1 0 0 1 0 1 0 1 1 0 1 1 1
*/
