// Digital circuit program_counter_8bit.dig as structural Verilog
module program_counter_8bit (
  input  sel,
  input  _7_in,
  input  _6_in,
  input  _5_in,
  input  _4_in,
  input  _3_in,
  input  _2_in,
  input  _1_in,
  input  _0_in,
  input  clk,
  input  reset,
  input  enable,
  output _7_out,
  output _6_out,
  output _5_out,
  output _4_out,
  output _3_out,
  output _2_out,
  output _1_out,
  output _0_out
);

  wire and_1_out, delay_1_out, delay_2_out, full_adder_8bit_1__0_out, full_adder_8bit_1__1_out,
       full_adder_8bit_1__2_out, full_adder_8bit_1__3_out, full_adder_8bit_1__4_out,
       full_adder_8bit_1__5_out, full_adder_8bit_1__6_out, full_adder_8bit_1__7_out, mux_8bit_1__0_out,
       mux_8bit_1__1_out, mux_8bit_1__2_out, mux_8bit_1__3_out, mux_8bit_1__4_out, mux_8bit_1__5_out,
       mux_8bit_1__6_out, mux_8bit_1__7_out;

  and and_1 (and_1_out, enable, sel);
  Delay #(.delayTime(5)) delay_1 (.in(clk), .out(delay_1_out));
  Delay #(.delayTime(3)) delay_2 (.in(reset), .out(delay_2_out));
  full_adder_8bit full_adder_8bit_1 (
    ._7a_in(_7_out), ._6a_in(_6_out), ._5a_in(_5_out), ._4a_in(_4_out), ._3a_in(_3_out), ._2a_in(_2_out),
    ._1a_in(_1_out), ._0a_in(_0_out), ._7b_in(1'b0), ._6b_in(1'b0), ._5b_in(1'b0), ._4b_in(1'b0),
    ._3b_in(1'b0), ._2b_in(1'b0), ._1b_in(1'b0), ._0b_in(1'b0), .carry_in(1'b1),
    ._7_out(full_adder_8bit_1__7_out), ._6_out(full_adder_8bit_1__6_out), ._5_out(full_adder_8bit_1__5_out),
    ._4_out(full_adder_8bit_1__4_out), ._3_out(full_adder_8bit_1__3_out), ._2_out(full_adder_8bit_1__2_out),
    ._1_out(full_adder_8bit_1__1_out), ._0_out(full_adder_8bit_1__0_out));  // open: carry_out
  mux_8bit mux_8bit_1 (
    .sel(and_1_out), ._7a_in(full_adder_8bit_1__7_out), ._6a_in(full_adder_8bit_1__6_out),
    ._5a_in(full_adder_8bit_1__5_out), ._4a_in(full_adder_8bit_1__4_out), ._3a_in(full_adder_8bit_1__3_out),
    ._2a_in(full_adder_8bit_1__2_out), ._1a_in(full_adder_8bit_1__1_out), ._0a_in(full_adder_8bit_1__0_out),
    ._7b_in(_7_in), ._6b_in(_6_in), ._5b_in(_5_in), ._4b_in(_4_in), ._3b_in(_3_in), ._2b_in(_2_in),
    ._1b_in(_1_in), ._0b_in(_0_in), ._7_out(mux_8bit_1__7_out), ._6_out(mux_8bit_1__6_out),
    ._5_out(mux_8bit_1__5_out), ._4_out(mux_8bit_1__4_out), ._3_out(mux_8bit_1__3_out),
    ._2_out(mux_8bit_1__2_out), ._1_out(mux_8bit_1__1_out), ._0_out(mux_8bit_1__0_out));
  register_8bit_falling register_8bit_falling_1 (
    ._7_in(mux_8bit_1__7_out), ._6_in(mux_8bit_1__6_out), ._5_in(mux_8bit_1__5_out),
    ._4_in(mux_8bit_1__4_out), ._3_in(mux_8bit_1__3_out), ._2_in(mux_8bit_1__2_out),
    ._1_in(mux_8bit_1__1_out), ._0_in(mux_8bit_1__0_out), .clk(delay_1_out), .reset(delay_2_out),
    ._7_out(_7_out), ._6_out(_6_out), ._5_out(_5_out), ._4_out(_4_out), ._3_out(_3_out), ._2_out(_2_out),
    ._1_out(_1_out), ._0_out(_0_out));

  // Notes on the sheet:
  //   reset: default 1
endmodule

/* Test case Program counter 8 bit:
enable sel 7_in 6_in 5_in 4_in 3_in 2_in 1_in 0_in clk reset 7_out 6_out 5_out 4_out 3_out 2_out 1_out 0_out
0 0 0 0 0 0 0 0 0 0 0 0  0 0 0 0 0 0 0 0
0 0 0 0 0 0 0 0 0 0 1 1  0 0 0 0 0 0 0 0
0 0 0 0 0 0 0 0 0 0 0 1  0 0 0 0 0 0 0 1
0 0 0 0 0 0 0 0 0 0 1 1  0 0 0 0 0 0 0 1
0 0 0 0 0 0 0 0 0 0 0 1  0 0 0 0 0 0 1 0
0 0 0 0 0 0 0 0 0 0 1 1  0 0 0 0 0 0 1 0
0 0 0 0 0 0 0 0 0 0 0 1  0 0 0 0 0 0 1 1
1 1 0 0 1 0 0 0 0 0 1 1  0 0 0 0 0 0 1 1
1 1 0 0 1 0 0 0 0 0 0 1  0 0 1 0 0 0 0 0
0 0 0 0 1 0 0 0 0 0 1 1  0 0 1 0 0 0 0 0
0 0 0 0 1 0 0 0 0 0 0 1  0 0 1 0 0 0 0 1
*/
