// Digital circuit register_8bit_falling.dig as structural Verilog
module register_8bit_falling (
  input  _7_in,
  input  _6_in,
  input  _5_in,
  input  _4_in,
  input  _3_in,
  input  _2_in,
  input  _1_in,
  input  _0_in,
  input  clk,
  input  reset,
  output _7_out,
  output _6_out,
  output _5_out,
  output _4_out,
  output _3_out,
  output _2_out,
  output _1_out,
  output _0_out
);

  d_trigger_falling_sync d_trigger_falling_sync_1 (.data(_7_in), .clk(clk), .reset(reset), .Q(_7_out));  // open: Q_2
  d_trigger_falling_sync d_trigger_falling_sync_2 (.data(_6_in), .clk(clk), .reset(reset), .Q(_6_out));  // open: Q_2
  d_trigger_falling_sync d_trigger_falling_sync_3 (.data(_5_in), .clk(clk), .reset(reset), .Q(_5_out));  // open: Q_2
  d_trigger_falling_sync d_trigger_falling_sync_4 (.data(_4_in), .clk(clk), .reset(reset), .Q(_4_out));  // open: Q_2
  d_trigger_falling_sync d_trigger_falling_sync_5 (.data(_3_in), .clk(clk), .reset(reset), .Q(_3_out));  // open: Q_2
  d_trigger_falling_sync d_trigger_falling_sync_6 (.data(_2_in), .clk(clk), .reset(reset), .Q(_2_out));  // open: Q_2
  d_trigger_falling_sync d_trigger_falling_sync_7 (.data(_1_in), .clk(clk), .reset(reset), .Q(_1_out));  // open: Q_2
  d_trigger_falling_sync d_trigger_falling_sync_8 (.data(_0_in), .clk(clk), .reset(reset), .Q(_0_out));  // open: Q_2

  // Notes on the sheet:
  //   Устойчивое начальное состояние симуляции Q=LOW, !Q=HIGH обеспечивает input resert=LOW по умолчанию
  //   Synchronous reset. Active LOW level
endmodule

/* Test case Register 8 bit. Falling edge:
7_in 6_in 5_in 4_in 3_in 2_in 1_in 0_in clk reset 7_out 6_out 5_out 4_out 3_out 2_out 1_out 0_out
0 0 0 0 0 0 0 0 0 0 0 0 0 0 0 0 0 0  
0 0 0 0 0 0 0 0 1 1 0 0 0 0 0 0 0 0 
1 1 1 1 1 1 1 1 1 1 0 0 0 0 0 0 0 0 
1 1 1 1 1 1 1 1 0 1 1 1 1 1 1 1 1 1  
1 1 1 1 1 1 1 1 0 0 0 0 0 0 0 0 0 0 
*/
