// Digital circuit register_8bit_falling_we_bus.dig as structural Verilog
module register_8bit_falling_we_bus (
  input  OE,
  input  WE,
  input  _7_in,
  input  _6_in,
  input  _5_in,
  input  _4_in,
  input  _3_in,
  input  _2_in,
  input  _1_in,
  input  _0_in,
  input  clk,
  input  reset,
  output _7_out,
  output _6_out,
  output _5_out,
  output _4_out,
  output _3_out,
  output _2_out,
  output _1_out,
  output _0_out,
  output [7:0] \reg 
);

  wire delay_1_out, delay_2_out, mux_8bit_1__0_out, mux_8bit_1__1_out, mux_8bit_1__2_out, mux_8bit_1__3_out,
       mux_8bit_1__4_out, mux_8bit_1__5_out, mux_8bit_1__6_out, mux_8bit_1__7_out, or_1_out, or_2_out;

  or or_1 (or_1_out, OE, 1'b0);
  or or_2 (or_2_out, WE, 1'b0);
  Delay #(.delayTime(5)) delay_1 (.in(clk), .out(delay_1_out));
  Delay #(.delayTime(3)) delay_2 (.in(reset), .out(delay_2_out));
  mux_8bit mux_8bit_1 (
    .sel(or_2_out), ._7a_in(\reg [7]), ._6a_in(\reg [6]), ._5a_in(\reg [5]), ._4a_in(\reg [4]),
    ._3a_in(\reg [3]), ._2a_in(\reg [2]), ._1a_in(\reg [1]), ._0a_in(\reg [0]), ._7b_in(_7_in),
    ._6b_in(_6_in), ._5b_in(_5_in), ._4b_in(_4_in), ._3b_in(_3_in), ._2b_in(_2_in), ._1b_in(_1_in),
    ._0b_in(_0_in), ._7_out(mux_8bit_1__7_out), ._6_out(mux_8bit_1__6_out), ._5_out(mux_8bit_1__5_out),
    ._4_out(mux_8bit_1__4_out), ._3_out(mux_8bit_1__3_out), ._2_out(mux_8bit_1__2_out),
    ._1_out(mux_8bit_1__1_out), ._0_out(mux_8bit_1__0_out));
  register_8bit_falling register_8bit_falling_1 (
    ._7_in(mux_8bit_1__7_out), ._6_in(mux_8bit_1__6_out), ._5_in(mux_8bit_1__5_out),
    ._4_in(mux_8bit_1__4_out), ._3_in(mux_8bit_1__3_out), ._2_in(mux_8bit_1__2_out),
    ._1_in(mux_8bit_1__1_out), ._0_in(mux_8bit_1__0_out), .clk(delay_1_out), .reset(delay_2_out),
    ._7_out(\reg [7]), ._6_out(\reg [6]), ._5_out(\reg [5]), ._4_out(\reg [4]), ._3_out(\reg [3]),
    ._2_out(\reg [2]), ._1_out(\reg [1]), ._0_out(\reg [0]));
  switch_8bit switch_8bit_1 (
    ._7_in(\reg [7]), ._6_in(\reg [6]), ._5_in(\reg [5]), ._4_in(\reg [4]), ._3_in(\reg [3]),
    ._2_in(\reg [2]), ._1_in(\reg [1]), ._0_in(\reg [0]), .sel(or_1_out), ._7_out(_7_out), ._6_out(_6_out),
    ._5_out(_5_out), ._4_out(_4_out), ._3_out(_3_out), ._2_out(_2_out), ._1_out(_1_out), ._0_out(_0_out));

  // Notes on the sheet:
  //   reset: default 1
  //   Для корректной работы регистра, вход reset должен стартовать на LOW уровне, но для режима записи reset должен быть на уровне HIGH
  //   Как избежать гонки данных.
  //   Что бы сработал WE, он должен первым принять состояние, 
  //   иначе после изменения CLK новые данные не будут учитываться.
  //    так как D-trigger работает по фронту, а не по уровню как D-latch.
  //   Для этого задержим сигнал clk на 5 единиц с помощью gate dalays
  //   При значении Z на входах OE и WE регистр имеет неопределенный нетестируемый выход!
  //   Переход в отключенное состояние OE=0, WE-0
  //   OE active HIGH level
  //   Reset active LOW level
endmodule

/* Test case Register falling edge. With WE and Bus:
OE WE 7_in 6_in 5_in 4_in 3_in 2_in 1_in 0_in clk reset 7_out 6_out 5_out 4_out 3_out 2_out 1_out 0_out
 0 0  0 0 0 0 0 0 0 0  0 0  Z Z Z Z Z Z Z Z
 0 1  0 0 0 0 0 0 0 0  0 0  Z Z Z Z Z Z Z Z
 1 1  0 0 0 0 0 0 0 0  0 0  0 0 0 0 0 0 0 0 
 1 0  1 0 0 0 0 0 0 0  1 1  0 0 0 0 0 0 0 0 

 1 1  1 0 0 0 0 0 0 0  0 1  1 0 0 0 0 0 0 0
 1 1  1 1 1 1 1 1 1 1  1 1  1 0 0 0 0 0 0 0
 1 1  1 1 1 1 1 1 1 1  0 1  1 1 1 1 1 1 1 1
 1 0  0 0 0 0 0 0 0 0  1 1  1 1 1 1 1 1 1 1
 1 0  0 0 0 0 0 0 0 0  0 1  1 1 1 1 1 1 1 1
 1 0  0 0 0 0 0 0 0 0  0 0  0 0 0 0 0 0 0 0
*/
