// Digital circuit register_8bit_rising.dig as structural Verilog
module register_8bit_rising (
  input  set,
  input  clk,
  input  reset,
  input  _7_in,
  input  _6_in,
  input  _5_in,
  input  _4_in,
  input  _3_in,
  input  _2_in,
  input  _1_in,
  input  _0_in,
  output _7_out,
  output _6_out,
  output _5_out,
  output _4_out,
  output _3_out,
  output _2_out,
  output _1_out,
  output _0_out
);

  d_trigger_rising_async d_trigger_rising_async_1 (
    .set(set), .clk(clk), .reset(reset), .data(_7_in), .Q(_7_out));  // open: Q_2
  d_trigger_rising_async d_trigger_rising_async_2 (
    .set(set), .clk(clk), .reset(reset), .data(_6_in), .Q(_6_out));  // open: Q_2
  d_trigger_rising_async d_trigger_rising_async_3 (
    .set(set), .clk(clk), .reset(reset), .data(_5_in), .Q(_5_out));  // open: Q_2
  d_trigger_rising_async d_trigger_rising_async_4 (
    .set(set), .clk(clk), .reset(reset), .data(_4_in), .Q(_4_out));  // open: Q_2
  d_trigger_rising_async d_trigger_rising_async_5 (
    .set(set), .clk(clk), .reset(reset), .data(_3_in), .Q(_3_out));  // open: Q_2
  d_trigger_rising_async d_trigger_rising_async_6 (
    .set(set), .clk(clk), .reset(reset), .data(_2_in), .Q(_2_out));  // open: Q_2
  d_trigger_rising_async d_trigger_rising_async_7 (
    .set(set), .clk(clk), .reset(reset), .data(_1_in), .Q(_1_out));  // open: Q_2
  d_trigger_rising_async d_trigger_rising_async_8 (
    .set(set), .clk(clk), .reset(reset), .data(_0_in), .Q(_0_out));  // open: Q_2

  // Notes on the sheet:
  //   set: default 1
  //   Устойчивое начальное состояние симуляции Q=LOW, !Q=HIGH обеспечивает input set=HIGH и resert=LOW по умолчанию
  //   Asynchronous set and reset. Active LOW level
endmodule

/* Test case Register 8 bit. Rising edge.:
set 7_in 6_in 5_in 4_in 3_in 2_in 1_in 0_in clk reset 7_out 6_out 5_out 4_out 3_out 2_out 1_out 0_out
0 0 0 0 0 0 0 0 0 0 1 1 1 1 1 1 1 1 1 
0 0 0 0 0 0 0 0 0 0 0 1 1 1 1 1 1 1 1 
1 0 0 0 0 0 0 0 0 0 0 0 0 0 0 0 0 0 0 
1 0 0 0 0 0 0 0 0 0 1 0 0 0 0 0 0 0 0 
1 1 1 1 1 1 1 1 1 0 1 0 0 0 0 0 0 0 0 
1 1 1 1 1 1 1 1 1 1 1 1 1 1 1 1 1 1 1 
1 1 1 1 1 1 1 1 1 0 1 1 1 1 1 1 1 1 1 
1 0 0 0 0 0 0 0 0 0 1 1 1 1 1 1 1 1 1 
1 0 0 0 0 0 0 0 0 1 1 0 0 0 0 0 0 0 0 
1 1 1 1 1 1 1 1 1 1 1 0 0 0 0 0 0 0 0 
1 1 1 1 1 1 1 1 1 0 1 0 0 0 0 0 0 0 0 
1 1 1 1 1 1 1 1 1 1 1 1 1 1 1 1 1 1 1 
*/
