// Digital circuit switch_8bit.dig as structural Verilog
module switch_8bit (
  input  _7_in,
  input  _6_in,
  input  _5_in,
  input  _4_in,
  input  _3_in,
  input  _2_in,
  input  _1_in,
  input  _0_in,
  input  sel,
  output _7_out,
  output _6_out,
  output _5_out,
  output _4_out,
  output _3_out,
  output _2_out,
  output _1_out,
  output _0_out
);

  wire or_1_out;

  or or_1 (or_1_out, sel, 1'b0);
  assign _7_out = or_1_out ? _7_in : 1'bz;  // Driver driver_1
  assign _6_out = or_1_out ? _6_in : 1'bz;  // Driver driver_2
  assign _5_out = or_1_out ? _5_in : 1'bz;  // Driver driver_3
  assign _4_out = or_1_out ? _4_in : 1'bz;  // Driver driver_4
  assign _3_out = or_1_out ? _3_in : 1'bz;  // Driver driver_5
  assign _2_out = or_1_out ? _2_in : 1'bz;  // Driver driver_6
  assign _1_out = or_1_out ? _1_in : 1'bz;  // Driver driver_7
  assign _0_out = or_1_out ? _0_in : 1'bz;  // Driver driver_8

  // Notes on the sheet:
  //   _7_in: pin 7
  //   _6_in: pin 6
  //   _5_in: pin 5
  //   _4_in: pin 4
  //   _3_in: pin 3
  //   _2_in: pin 2
  //   _1_in: pin 1
  //   sel: pin 8
  //   _7_out: pin 7
  //   _6_out: pin 6
  //   _5_out: pin 5
  //   _4_out: pin 4
  //   _3_out: pin 3
  //   _2_out: pin 2
  //   _1_out: pin 1
endmodule

/* Test case Switch 8 bit HIGH level:
sel 7_in 6_in 5_in 4_in 3_in 2_in 1_in 0_in 7_out 6_out 5_out 4_out 3_out 2_out 1_out 0_out   
1 1 1 1 1 1 1 1 1 1 1 1 1 1 1 1 1
0 1 1 1 1 1 1 1 1 Z Z Z Z Z Z Z Z
0 0 0 0 0 0 0 0 0 Z Z Z Z Z Z Z Z
*/
