// Digital circuit turing_complete_cpu_falling.dig as structural Verilog
module turing_complete_cpu_falling (
  input  reset_c,
  input  _7_in,
  input  _6_in,
  input  _5_in,
  input  _4_in,
  input  _3_in,
  input  _2_in,
  input  _1_in,
  input  _0_in,
  input  clk,
  input  reset,
  output [7:0] out_1,
  output [7:0] out_3,
  output out_13,
  output out_14,
  output out_15,
  output out_16,
  output out_17,
  output out_19,
  output out_20,
  output [7:0] out_21,
  output [7:0] out_22,
  output [7:0] out_23
);

  wire dec_3_8_1__001, dec_3_8_1__110, dec_3_8_2__001, dec_3_8_2__010, dec_3_8_2__011, dec_3_8_2__100,
       dec_3_8_2__101, dec_3_8_2__111, not_1_out, switch_8bit_1__0_out, switch_8bit_1__1_out,
       switch_8bit_1__2_out, switch_8bit_1__3_out, switch_8bit_1__4_out, switch_8bit_1__5_out,
       switch_8bit_1__6_out, switch_8bit_1__7_out;

  ROM #(.AddrBits(8), .Bits(8)) rom_1 (.A(out_1), .sel(1'b1), .D(out_3));
  not not_1 (not_1_out, clk);
  Counter #(.Bits(8)) counter_1 (.en(1'b1), .C(not_1_out), .clr(reset_c), .out(out_1));  // open: ovf
  switch_8bit switch_8bit_1 (
    ._7_in(_7_in), ._6_in(_6_in), ._5_in(_5_in), ._4_in(_4_in), ._3_in(_3_in), ._2_in(_2_in), ._1_in(_1_in),
    ._0_in(_0_in), .sel(dec_3_8_1__110), ._7_out(switch_8bit_1__7_out), ._6_out(switch_8bit_1__6_out),
    ._5_out(switch_8bit_1__5_out), ._4_out(switch_8bit_1__4_out), ._3_out(switch_8bit_1__3_out),
    ._2_out(switch_8bit_1__2_out), ._1_out(switch_8bit_1__1_out), ._0_out(switch_8bit_1__0_out));
  switch_8bit switch_8bit_2 (
    ._7_in(switch_8bit_1__7_out), ._6_in(switch_8bit_1__6_out), ._5_in(switch_8bit_1__5_out),
    ._4_in(switch_8bit_1__4_out), ._3_in(switch_8bit_1__3_out), ._2_in(switch_8bit_1__2_out),
    ._1_in(switch_8bit_1__1_out), ._0_in(switch_8bit_1__0_out), .sel(out_20), ._7_out(out_21[7]),
    ._6_out(out_21[6]), ._5_out(out_21[5]), ._4_out(out_21[4]), ._3_out(out_21[3]), ._2_out(out_21[2]),
    ._1_out(out_21[1]), ._0_out(out_21[0]));
  dec_3_8 dec_3_8_1 (
    ._2_in(out_3[5]), ._1_in(out_3[4]), ._0_in(out_3[3]), ._110(dec_3_8_1__110), ._101(out_13),
    ._100(out_14), ._011(out_15), ._010(out_16), ._001(dec_3_8_1__001), ._000(out_17));  // open: _111
  dec_3_8 dec_3_8_2 (
    ._2_in(out_3[2]), ._1_in(out_3[1]), ._0_in(out_3[0]), ._111(dec_3_8_2__111), ._110(out_20),
    ._101(dec_3_8_2__101), ._100(dec_3_8_2__100), ._011(dec_3_8_2__011), ._010(dec_3_8_2__010),
    ._001(dec_3_8_2__001), ._000(out_19));
  register_8bit_falling_we_bus register_8bit_falling_we_bus_1 (
    .OE(out_17), .WE(out_19), ._7_in(switch_8bit_1__7_out), ._6_in(switch_8bit_1__6_out),
    ._5_in(switch_8bit_1__5_out), ._4_in(switch_8bit_1__4_out), ._3_in(switch_8bit_1__3_out),
    ._2_in(switch_8bit_1__2_out), ._1_in(switch_8bit_1__1_out), ._0_in(switch_8bit_1__0_out), .clk(clk),
    .reset(reset), .\reg (out_22), ._7_out(switch_8bit_1__7_out), ._6_out(switch_8bit_1__6_out),
    ._5_out(switch_8bit_1__5_out), ._4_out(switch_8bit_1__4_out), ._3_out(switch_8bit_1__3_out),
    ._2_out(switch_8bit_1__2_out), ._1_out(switch_8bit_1__1_out), ._0_out(switch_8bit_1__0_out));
  register_8bit_falling_we_bus register_8bit_falling_we_bus_2 (
    .OE(dec_3_8_1__001), .WE(dec_3_8_2__001), ._7_in(switch_8bit_1__7_out), ._6_in(switch_8bit_1__6_out),
    ._5_in(switch_8bit_1__5_out), ._4_in(switch_8bit_1__4_out), ._3_in(switch_8bit_1__3_out),
    ._2_in(switch_8bit_1__2_out), ._1_in(switch_8bit_1__1_out), ._0_in(switch_8bit_1__0_out), .clk(clk),
    .reset(reset), .\reg (out_23), ._7_out(switch_8bit_1__0_out), ._6_out(switch_8bit_1__1_out),
    ._5_out(switch_8bit_1__2_out), ._4_out(switch_8bit_1__3_out), ._3_out(switch_8bit_1__4_out),
    ._2_out(switch_8bit_1__5_out), ._1_out(switch_8bit_1__6_out), ._0_out(switch_8bit_1__7_out));

  // Notes on the sheet:
  //   _2_in: default 1
  //   _1_in: default 1
  //   _0_in: default 1
  //   reset: default 1
  //   contents of rom_1 (hex, n*v repeats v):
  //   0,b0,86
  //   Source
  //   Destination
  //   INPUT
  //   REG 5
  //   REG 4
  //   REG 3
  //   REG 2
  //   REG 1
  //   REG 0
  //   OUT
  //   Main
endmodule
