// Digital circuit turing_complete_cpu_rising.dig as structural Verilog
module turing_complete_cpu_rising (
  input  _7_in,
  input  _6_in,
  input  _5_in,
  input  _4_in,
  input  _3_in,
  input  _2_in,
  input  _1_in,
  input  _0_in,
  input  clk,
  input  reset,
  output [7:0] out_1,
  output [7:0] out,
  output [7:0] out_13,
  output [7:0] out_14,
  output [7:0] out_15,
  output [7:0] out_16,
  output [7:0] out_17,
  output [7:0] out_18,
  output [7:0] out_19,
  output out_20,
  output [7:0] out_21
);

  wire alu_1__0_out, alu_1__1_out, alu_1__2_out, alu_1__3_out, alu_1__4_out, alu_1__5_out, alu_1__6_out,
       alu_1__7_out, and_1_out, dec_2_4_1__00, dec_2_4_1__01, dec_2_4_1__10, dec_2_4_1__11,
       dec_3_8_disable_1__000, dec_3_8_disable_1__001, dec_3_8_disable_1__010, dec_3_8_disable_1__011,
       dec_3_8_disable_1__100, dec_3_8_disable_1__101, dec_3_8_disable_1__110, dec_3_8_disable_2__000,
       dec_3_8_disable_2__001, dec_3_8_disable_2__010, dec_3_8_disable_2__011, dec_3_8_disable_2__100,
       dec_3_8_disable_2__101, dec_3_8_disable_2__110, mux_8bit_1__0_out, mux_8bit_1__1_out,
       mux_8bit_1__2_out, mux_8bit_1__3_out, mux_8bit_1__4_out, mux_8bit_1__5_out, mux_8bit_1__6_out,
       mux_8bit_1__7_out, mux_8bit_z_1__0_out, mux_8bit_z_1__1_out, mux_8bit_z_1__2_out, mux_8bit_z_1__3_out,
       mux_8bit_z_1__4_out, mux_8bit_z_1__5_out, mux_8bit_z_1__6_out, mux_8bit_z_1__7_out, not_1_out,
       or_1_out, or_2_out, or_3_out;

  conditions conditions_1 (
    ._2_addr(out_1[2]), ._1_addr(out_1[1]), ._0_addr(out_1[0]), ._7_in(out_16[7]), ._6_in(out_16[6]),
    ._5_in(out_16[5]), ._4_in(out_16[4]), ._3_in(out_16[3]), ._2_in(out_16[2]), ._1_in(out_16[1]),
    ._0_in(out_16[0]), .out(out_20));
  program_counter_8bit program_counter_8bit_1 (
    .sel(out_20), ._7_in(out_13[7]), ._6_in(out_13[6]), ._5_in(out_13[5]), ._4_in(out_13[4]),
    ._3_in(out_13[3]), ._2_in(out_13[2]), ._1_in(out_13[1]), ._0_in(out_13[0]), .clk(clk), .reset(reset),
    .enable(dec_2_4_1__11), ._7_out(out_21[7]), ._6_out(out_21[6]), ._5_out(out_21[5]), ._4_out(out_21[4]),
    ._3_out(out_21[3]), ._2_out(out_21[2]), ._1_out(out_21[1]), ._0_out(out_21[0]));
  ROM #(.AddrBits(8), .Bits(8)) rom_1 (.A(out_21), .sel(1'b1), .D(out_1));
  switch_8bit switch_8bit_1 (
    ._7_in(_7_in), ._6_in(_6_in), ._5_in(_5_in), ._4_in(_4_in), ._3_in(_3_in), ._2_in(_2_in), ._1_in(_1_in),
    ._0_in(_0_in), .sel(dec_3_8_disable_1__110), ._7_out(out_19[7]), ._6_out(out_19[6]), ._5_out(out_19[5]),
    ._4_out(out_19[4]), ._3_out(out_19[3]), ._2_out(out_19[2]), ._1_out(out_19[1]), ._0_out(out_19[0]));
  switch_8bit switch_8bit_2 (
    ._7_in(out_19[7]), ._6_in(out_19[6]), ._5_in(out_19[5]), ._4_in(out_19[4]), ._3_in(out_19[3]),
    ._2_in(out_19[2]), ._1_in(out_19[1]), ._0_in(out_19[0]), .sel(dec_3_8_disable_2__110), ._7_out(out[7]),
    ._6_out(out[6]), ._5_out(out[5]), ._4_out(out[4]), ._3_out(out[3]), ._2_out(out[2]), ._1_out(out[1]),
    ._0_out(out[0]));
  dec_2_4 dec_2_4_1 (
    ._1_in(out_1[7]), ._0_in(out_1[6]), ._11(dec_2_4_1__11), ._10(dec_2_4_1__10), ._01(dec_2_4_1__01),
    ._00(dec_2_4_1__00));
  dec_3_8_disable dec_3_8_disable_1 (
    .sel(and_1_out), ._2_in(out_1[5]), ._1_in(out_1[4]), ._0_in(out_1[3]), ._110(dec_3_8_disable_1__110),
    ._101(dec_3_8_disable_1__101), ._100(dec_3_8_disable_1__100), ._011(dec_3_8_disable_1__011),
    ._010(dec_3_8_disable_1__010), ._001(dec_3_8_disable_1__001), ._000(dec_3_8_disable_1__000));  // open: _111
  dec_3_8_disable dec_3_8_disable_2 (
    .sel(and_1_out), ._2_in(out_1[2]), ._1_in(out_1[1]), ._0_in(out_1[0]), ._110(dec_3_8_disable_2__110),
    ._101(dec_3_8_disable_2__101), ._100(dec_3_8_disable_2__100), ._011(dec_3_8_disable_2__011),
    ._010(dec_3_8_disable_2__010), ._001(dec_3_8_disable_2__001), ._000(dec_3_8_disable_2__000));  // open: _111
  mux_8bit mux_8bit_1 (
    .sel(dec_2_4_1__00), ._7a_in(out_1[7]), ._6a_in(out_1[6]), ._5a_in(out_1[5]), ._4a_in(out_1[4]),
    ._3a_in(out_1[3]), ._2a_in(out_1[2]), ._1a_in(out_1[1]), ._0a_in(out_1[0]), ._7b_in(1'b0), ._6b_in(1'b0),
    ._5b_in(out_1[5]), ._4b_in(out_1[4]), ._3b_in(out_1[3]), ._2b_in(out_1[2]), ._1b_in(out_1[1]),
    ._0b_in(out_1[0]), ._7_out(mux_8bit_1__7_out), ._6_out(mux_8bit_1__6_out), ._5_out(mux_8bit_1__5_out),
    ._4_out(mux_8bit_1__4_out), ._3_out(mux_8bit_1__3_out), ._2_out(mux_8bit_1__2_out),
    ._1_out(mux_8bit_1__1_out), ._0_out(mux_8bit_1__0_out));
  not not_1 (not_1_out, or_1_out);
  and and_1 (and_1_out, not_1_out, dec_2_4_1__10);
  or or_1 (or_1_out, dec_2_4_1__01, dec_2_4_1__11, dec_2_4_1__00);
  or or_2 (or_2_out, dec_3_8_disable_2__000, dec_2_4_1__00);
  register_8bit_rising_we_bus register_8bit_rising_we_bus_1 (
    .OE(dec_3_8_disable_1__000), .WE(or_2_out), ._7_in(mux_8bit_1__7_out), ._6_in(mux_8bit_1__6_out),
    ._5_in(mux_8bit_1__5_out), ._4_in(mux_8bit_1__4_out), ._3_in(mux_8bit_1__3_out),
    ._2_in(mux_8bit_1__2_out), ._1_in(mux_8bit_1__1_out), ._0_in(mux_8bit_1__0_out), .clk(clk),
    .reset(reset), .\reg (out_13), ._7_out(out_19[7]), ._6_out(out_19[6]), ._5_out(out_19[5]),
    ._4_out(out_19[4]), ._3_out(out_19[3]), ._2_out(out_19[2]), ._1_out(out_19[1]), ._0_out(out_19[0]));
  register_8bit_rising_we_bus register_8bit_rising_we_bus_2 (
    .OE(dec_3_8_disable_1__001), .WE(dec_3_8_disable_2__001), ._7_in(out_19[7]), ._6_in(out_19[6]),
    ._5_in(out_19[5]), ._4_in(out_19[4]), ._3_in(out_19[3]), ._2_in(out_19[2]), ._1_in(out_19[1]),
    ._0_in(out_19[0]), .clk(clk), .reset(reset), .\reg (out_14), ._7_out(out_19[7]), ._6_out(out_19[6]),
    ._5_out(out_19[5]), ._4_out(out_19[4]), ._3_out(out_19[3]), ._2_out(out_19[2]), ._1_out(out_19[1]),
    ._0_out(out_19[0]));
  register_8bit_rising_we_bus register_8bit_rising_we_bus_3 (
    .OE(dec_3_8_disable_1__010), .WE(dec_3_8_disable_2__010), ._7_in(out_19[7]), ._6_in(out_19[6]),
    ._5_in(out_19[5]), ._4_in(out_19[4]), ._3_in(out_19[3]), ._2_in(out_19[2]), ._1_in(out_19[1]),
    ._0_in(out_19[0]), .clk(clk), .reset(reset), .\reg (out_15), ._7_out(out_19[7]), ._6_out(out_19[6]),
    ._5_out(out_19[5]), ._4_out(out_19[4]), ._3_out(out_19[3]), ._2_out(out_19[2]), ._1_out(out_19[1]),
    ._0_out(out_19[0]));
  alu alu_1 (
    ._2_addr(out_1[2]), ._1_addr(out_1[1]), ._0_addr(out_1[0]), ._7a_in(out_14[7]), ._6a_in(out_14[6]),
    ._5a_in(out_14[5]), ._4a_in(out_14[4]), ._3a_in(out_14[3]), ._2a_in(out_14[2]), ._1a_in(out_14[1]),
    ._0a_in(out_14[0]), ._7b_in(out_15[7]), ._6b_in(out_15[6]), ._5b_in(out_15[5]), ._4b_in(out_15[4]),
    ._3b_in(out_15[3]), ._2b_in(out_15[2]), ._1b_in(out_15[1]), ._0b_in(out_15[0]), ._7_out(alu_1__7_out),
    ._6_out(alu_1__6_out), ._5_out(alu_1__5_out), ._4_out(alu_1__4_out), ._3_out(alu_1__3_out),
    ._2_out(alu_1__2_out), ._1_out(alu_1__1_out), ._0_out(alu_1__0_out));  // open: carry_neg, carry_sub, carry_add
  mux_8bit_Z mux_8bit_z_1 (
    .sel(dec_2_4_1__01), ._7a_in(out_19[7]), ._6a_in(out_19[6]), ._5a_in(out_19[5]), ._4a_in(out_19[4]),
    ._3a_in(out_19[3]), ._2a_in(out_19[2]), ._1a_in(out_19[1]), ._0a_in(out_19[0]), ._7b_in(alu_1__7_out),
    ._6b_in(alu_1__6_out), ._5b_in(alu_1__5_out), ._4b_in(alu_1__4_out), ._3b_in(alu_1__3_out),
    ._2b_in(alu_1__2_out), ._1b_in(alu_1__1_out), ._0b_in(alu_1__0_out), ._7_out(mux_8bit_z_1__7_out),
    ._6_out(mux_8bit_z_1__6_out), ._5_out(mux_8bit_z_1__5_out), ._4_out(mux_8bit_z_1__4_out),
    ._3_out(mux_8bit_z_1__3_out), ._2_out(mux_8bit_z_1__2_out), ._1_out(mux_8bit_z_1__1_out),
    ._0_out(mux_8bit_z_1__0_out));
  or or_3 (or_3_out, dec_2_4_1__01, dec_3_8_disable_2__011);
  register_8bit_rising_we_bus register_8bit_rising_we_bus_4 (
    .OE(dec_3_8_disable_1__011), .WE(or_3_out), ._7_in(mux_8bit_z_1__7_out), ._6_in(mux_8bit_z_1__6_out),
    ._5_in(mux_8bit_z_1__5_out), ._4_in(mux_8bit_z_1__4_out), ._3_in(mux_8bit_z_1__3_out),
    ._2_in(mux_8bit_z_1__2_out), ._1_in(mux_8bit_z_1__1_out), ._0_in(mux_8bit_z_1__0_out), .clk(clk),
    .reset(reset), .\reg (out_16), ._7_out(out_19[7]), ._6_out(out_19[6]), ._5_out(out_19[5]),
    ._4_out(out_19[4]), ._3_out(out_19[3]), ._2_out(out_19[2]), ._1_out(out_19[1]), ._0_out(out_19[0]));
  register_8bit_rising_we_bus register_8bit_rising_we_bus_5 (
    .OE(dec_3_8_disable_1__100), .WE(dec_3_8_disable_2__100), ._7_in(out_19[7]), ._6_in(out_19[6]),
    ._5_in(out_19[5]), ._4_in(out_19[4]), ._3_in(out_19[3]), ._2_in(out_19[2]), ._1_in(out_19[1]),
    ._0_in(out_19[0]), .clk(clk), .reset(reset), .\reg (out_17), ._7_out(out_19[7]), ._6_out(out_19[6]),
    ._5_out(out_19[5]), ._4_out(out_19[4]), ._3_out(out_19[3]), ._2_out(out_19[2]), ._1_out(out_19[1]),
    ._0_out(out_19[0]));
  register_8bit_rising_we_bus register_8bit_rising_we_bus_6 (
    .OE(dec_3_8_disable_1__101), .WE(dec_3_8_disable_2__101), ._7_in(out_19[7]), ._6_in(out_19[6]),
    ._5_in(out_19[5]), ._4_in(out_19[4]), ._3_in(out_19[3]), ._2_in(out_19[2]), ._1_in(out_19[1]),
    ._0_in(out_19[0]), .clk(clk), .reset(reset), .\reg (out_18), ._7_out(out_19[7]), ._6_out(out_19[6]),
    ._5_out(out_19[5]), ._4_out(out_19[4]), ._3_out(out_19[3]), ._2_out(out_19[2]), ._1_out(out_19[1]),
    ._0_out(out_19[0]));

  // Notes on the sheet:
  //   _2_in: default 1
  //   _1_in: default 1
  //   _0_in: default 1
  //   reset: default 1
  //   Input
  //   Output
  //   Debug 
  //   conditions
  //   contents of rom_1 (hex, n*v repeats v):
  //   0,b1,1,82,44,9e,c6,ff
  //   Debug 
  //   counter
  //   Instruction
  //   Debug bus
  //   Source
  //   Destination
  //   conditions
  //   copy
  //   calc
  //   immediate values
  //   INPUT
  //   REG 5
  //   REG 4
  //   REG 3
  //   REG 2
  //   REG 1
  //   REG 0
  //   OUT
  //   Debug REG 0
  //   Debug REG 1
  //   Debug REG 2
  //   Debug REG 3
  //   Debug REG 4
  //   Debug REG 5
endmodule
